// Logisim project final-project.circ as structural Verilog: 23 circuits, main circuit processor
module main (
  input  reset,
  output loss,
  output win
);

  wire and_1_out, clk, controlled_buffer_1_out, module_1_solved, module_2_solved, not_1_out, not_2_out,
       ready, start, started, x_m_swtc, x_m_swtp;
  wire [3:0] module_addr;
  wire [15:0] \time ;
  wire [31:0] module_data;

  Clock u_clk (.out(clk));
  LED led_1 (.in(ready));
  Button PUSH_TO_START (.out(start));
  LED led_2 (.in(module_1_solved));
  card_matching card_matching_1 (
    .reset(reset), .wr_en(x_m_swtc), .Solved(module_1_solved), .in_4(module_data[3:0]), .in_2(module_addr),
    .clk(clk), .\time (\time ));
  LED led_3 (.in(module_2_solved));
  pattern_memory pattern_memory_1 (
    .data(module_data), .wr_en(x_m_swtp), .clr(reset), .solved(module_2_solved), .clk(clk), .\time (\time ));
  assign controlled_buffer_1_out = loss ? 1'b1 : 1'bz;  // Controlled_Buffer controlled_buffer_1
  Hex_Digit_Display hex_digit_display_1 (.value(\time [11:8]), .dp(1'b1));
  Hex_Digit_Display hex_digit_display_2 (.value(\time [15:12]));  // open: dp
  Hex_Digit_Display hex_digit_display_3 (.value(\time [3:0]));  // open: dp
  Hex_Digit_Display hex_digit_display_4 (.value(\time [7:4]));  // open: dp
  and and_1 (and_1_out, clk, not_1_out, not_2_out, started);
  not not_1 (not_1_out, win);
  not not_2 (not_2_out, loss);
  game_over game_over_1 (.\time (\time ), .game_over(loss), .reset(reset));
  D_Flip_Flop #(.trigger("high")) d_ff_1 (
    .clk(x_m_swtp), .D(x_m_swtp), .Q(ready), .en(x_m_swtp), .reset(reset));  // open: Qn, preset
  processor processor_1 (
    .reset(reset), .x_m_swtc(x_m_swtc), .x_m_swtp(x_m_swtp), .module_addr(module_addr),
    .module_data(module_data), .clk(clk));
  timer timer_1 (
    .clr(reset), .sec_d1(\time [3:0]), .sec_d2(\time [7:4]), .min_d1(\time [11:8]), .min_d2(\time [15:12]),
    .clk(and_1_out));
  winner winner_1 (.module_1(module_1_solved), .module_2(module_2_solved), .reset(reset), .game_won(win));
  D_Flip_Flop #(.trigger("high")) d_ff_2 (
    .clk(start), .D(start), .Q(started), .en(ready), .reset(reset));  // open: Qn, preset
  // also tied to GND on the sheet: controlled_buffer_1_out

  // Other names for the same wires on the sheet: GAME_OVER = loss; YOU_WIN = win

  // Notes on the sheet:
  //   After LED below gives the signal, you may begin.
  //   MODULE 1: CARD-MATCHING
  //   double click on the module below to begin solving it
  //   MODULE 2: PATTERN MEMORY
  //   double click on the module below to begin solving it
  //   WELCOME, PLAYER
  //   For my final project, I have created a BOMB.
  //   You have 2 minutes to solve the following two modules in order to defuse the bomb.
  //   Failure to defuse the bomb in time will result in a... SHORT CIRCUIT.
  //   ECE350
endmodule

// 0
module processor (
  input  clk,
  input  reset,
  output x_m_swtc,
  output x_m_swtp,
  output [3:0] module_addr,
  output [31:0] module_data
);

  wire alu_lt, alu_ne, alu_ovf, and_1_out, and_2_out, and_3_out, and_4_out, and_5_out, bex_m_x_bypass,
       d_x_add, d_x_addi, d_x_and, d_x_bex, d_x_blt, d_x_bne, d_x_br, d_x_j, d_x_j____jal____jr, d_x_jal,
       d_x_jr, d_x_lw, d_x_N____B, d_x_nop, d_x_or, d_x_r, d_x_rand, d_x_rd_rt, d_x_rs1_____r0,
       d_x_rs1____m_w_rd, d_x_rs1____x_m_rd, d_x_rs2_____r0, d_x_rs2____m_w_rd, d_x_rs2____x_m_rd, d_x_sa,
       d_x_setx, d_x_sll, d_x_sub, d_x_sw, d_x_swtc, d_x_swtp, d_x_writes, f_d_addi, f_d_bex, f_d_blt,
       f_d_bne, f_d_j, f_d_jal, f_d_jr, f_d_lw, f_d_nop, f_d_r, f_d_rand, f_d_rd_rt, f_d_rs1_____r0,
       f_d_rs1____d_x_rd, f_d_rs1____x_m_rd, f_d_rs2_____r0, f_d_rs2____d_x_rd, f_d_rs2____x_m_rd, f_d_setx,
       f_d_sw, f_d_swtc, f_d_swtp, m_w_addi, m_w_bex, m_w_blt, m_w_bne, m_w_j, m_w_jal, m_w_jr, m_w_lw,
       m_w_r, m_w_rand, m_w_setx, m_w_sw, m_w_swtc, m_w_swtp, m_w_writes, n5_bit_equal_1_isequal,
       n5_bit_equal_2_isequal, n5_bit_equal_3_isequal, n5_bit_equal_4_isequal, n5_bit_equal_9_isequal,
       n5_bit_equal_10_isequal, n5_bit_equal_11_isequal, n5_bit_equal_12_isequal, n5_bit_equal_13_isequal,
       need_subtraction, not_1_out, not_2_out, not_3_out, not_4_out, not_5_out, not_6_out, not_7_out,
       not_8_out, not_9_out, not_10_out, not_11_out, not_12_out, not_13_out, or_1_out, or_7_out, overflow,
       stall, x_m_addi, x_m_bex, x_m_blt, x_m_bne, x_m_j, x_m_jal, x_m_jr, x_m_lw, x_m_r, x_m_rand,
       x_m_rd_rt, x_m_rs2_____r0, x_m_rs2____m_w_rd, x_m_setx, x_m_sw, x_m_writes;
  wire [4:0] alu_op, alu_op_in, d_x_rs1, d_x_rs2, f_d_rs1, f_d_rs2, multiplexer_4_out, multiplexer_11_out,
       multiplexer_20_out_2, multiplexer_21_out, multiplexer_29_out, rf_wreg, x_m_rs2;
  wire [11:0] multiplexer_1_out, multiplexer_2_out;
  wire [26:0] rstatus;
  wire [31:0] alu_1_out_8, bit_extender_1_out, bit_extender_2_out, bit_extender_3_out, bit_extender_4_out,
       br_address, D_X_A_output, D_X_B_output, d_x_ir, d_x_j_address, D_X_PC_output, f_d_ir, F_D_PC_output,
       M_W_D_output, m_w_ir, M_W_O_output, multiplexer_3_out, multiplexer_7_out, multiplexer_12_out,
       multiplexer_13_out, multiplexer_14_out, multiplexer_15_out, multiplexer_16_out, multiplexer_17_out,
       multiplexer_18_out, multiplexer_19_out, multiplexer_20_out, multiplexer_24_out, multiplexer_25_out,
       multiplexer_28_out, n32_bit_compact_1_result, n32_bit_compact_2_result, PC_output, ram_1_data,
       random_1_out, RegisterFile_readdata1, RegisterFile_readdata2, rf_wdata, rom_1_data, X_M_B_output;
  wire [31:4] x_m_o;
  wire [31:27] x_m_ir;

  not not_1 (not_1_out, stall);
  Multiplexer #(.width(12), .enable("false")) multiplexer_1 (
    .in0(multiplexer_2_out), .in1(br_address[11:0]), .out(multiplexer_1_out), .sel(d_x_br));
  register_32 PC (.clk(clk), .\input (bit_extender_1_out), .enable(not_1_out), .\output (PC_output), .reset(reset));
  assign bit_extender_1_out = {{20{1'b0}}, multiplexer_1_out};  // Bit_Extender bit_extender_1
  Multiplexer #(.width(12), .enable("false")) multiplexer_2 (
    .in0(n32_bit_compact_1_result[11:0]), .in1(d_x_j_address[11:0]), .out(multiplexer_2_out),
    .sel(d_x_j____jal____jr));
  _32_bit_compact u_32_bit_compact_1 (
    .result(n32_bit_compact_1_result), .A(PC_output), .B(32'h1), .sub(1'b0));  // open: ovf
  ROM #(.addrWidth(12), .dataWidth(32)) rom_1 (.addr(PC_output[11:0]), .data(rom_1_data));  // open: sel
  // Probe on rom_1_data
  not not_2 (not_2_out, f_d_sw);
  or or_1 (or_1_out, not_2_out, not_3_out, not_4_out);
  not not_3 (not_3_out, f_d_swtc);
  not not_4 (not_4_out, f_d_swtp);
  Multiplexer #(.width(32), .enable("false")) multiplexer_3 (
    .in0(rom_1_data), .in1({32{1'b0}}), .out(multiplexer_3_out), .sel(f_d_nop));
  not not_5 (not_5_out, stall);
  and and_1 (and_1_out, f_d_lw, f_d_rs1____d_x_rd);
  and and_2 (and_2_out, or_1_out, f_d_rs2____d_x_rd);
  or or_2 (d_x_nop, d_x_br, d_x_j____jal____jr, stall);
  or or_3 (f_d_nop, d_x_br, d_x_j____jal____jr);
  not not_6 (not_6_out, clk);
  register_32 F_D_PC (
    .clk(clk), .\input (n32_bit_compact_1_result), .enable(not_5_out), .\output (F_D_PC_output), .reset(reset));
  register_32 u_F_D_IR (.clk(clk), .\input (multiplexer_3_out), .enable(not_5_out), .\output (f_d_ir), .reset(reset));
  // Probe on rf_wreg
  // Probe on rf_wdata
  or or_4 (stall, and_1_out, and_2_out);
  or or_5 (d_x_br, and_3_out, and_4_out, and_5_out);
  decoder decoder_1 (
    .opcode(f_d_ir[31:27]), .r(f_d_r), .addi(f_d_addi), .sw(f_d_sw), .lw(f_d_lw), .j(f_d_j), .bne(f_d_bne),
    .jal(f_d_jal), .jr(f_d_jr), .blt(f_d_blt), .bex(f_d_bex), .setx(f_d_setx), .swtp(f_d_swtp),
    .swtc(f_d_swtc), .\rand (f_d_rand));
  or or_6 (f_d_rd_rt, f_d_bne, f_d_blt, f_d_swtp, f_d_jr, f_d_sw, f_d_swtc);
  _5_bit_equal u_5_bit_equal_1 (.A(f_d_rs1), .B(d_x_ir[26:22]), .isEqual(n5_bit_equal_1_isequal));
  _5_bit_equal u_5_bit_equal_2 (.A(f_d_rs1), .B(rstatus[26:22]), .isEqual(n5_bit_equal_2_isequal));
  _5_bit_equal u_5_bit_equal_3 (.A(f_d_rs2), .B(rstatus[26:22]), .isEqual(n5_bit_equal_3_isequal));
  _5_bit_equal u_5_bit_equal_4 (.A(f_d_rs2), .B(d_x_ir[26:22]), .isEqual(n5_bit_equal_4_isequal));
  and and_3 (and_3_out, d_x_bex, alu_ne);
  and and_4 (and_4_out, d_x_bne, alu_ne);
  and and_5 (and_5_out, d_x_blt, not_7_out, alu_ne);
  RegisterFile RegisterFile (
    .WriteReg(rf_wreg), .WriteData(rf_wdata), .RegWriteEnable(m_w_writes), .clk(not_6_out), .reset(reset),
    .ReadData2(RegisterFile_readdata2), .ReadReg2(f_d_rs2), .ReadReg1(f_d_rs1),
    .ReadData1(RegisterFile_readdata1));
  not not_7 (not_7_out, alu_lt);
  Multiplexer #(.width(5), .enable("false")) multiplexer_4 (
    .in0(f_d_ir[16:12]), .in1(f_d_ir[26:22]), .out(multiplexer_4_out), .sel(f_d_rd_rt));
  not not_8 (not_8_out, f_d_rs1_____r0);
  not not_9 (not_9_out, f_d_rs2_____r0);
  Multiplexer #(.width(5), .enable("false")) multiplexer_5 (
    .in0(f_d_ir[21:17]), .in1({5{1'b0}}), .out(f_d_rs1), .sel(f_d_bex));
  Multiplexer #(.width(5), .enable("false")) multiplexer_6 (
    .in0(multiplexer_4_out), .in1(5'b11110), .out(f_d_rs2), .sel(f_d_bex));
  and and_6 (f_d_rs1____d_x_rd, n5_bit_equal_1_isequal, d_x_writes, not_8_out);
  and and_7 (f_d_rs1____x_m_rd, n5_bit_equal_2_isequal, x_m_writes, not_8_out);
  and and_8 (f_d_rs2____x_m_rd, n5_bit_equal_3_isequal, x_m_writes, not_9_out);
  and and_9 (f_d_rs2____d_x_rd, n5_bit_equal_4_isequal, d_x_writes, not_9_out);
  _5_bit_equal u_5_bit_equal_5 (.A(f_d_rs1), .B({5{1'b0}}), .isEqual(f_d_rs1_____r0));
  _5_bit_equal u_5_bit_equal_6 (.A(f_d_rs2), .B({5{1'b0}}), .isEqual(f_d_rs2_____r0));
  Multiplexer #(.width(32), .enable("false")) multiplexer_7 (
    .in0(f_d_ir), .in1({32{1'b0}}), .out(multiplexer_7_out), .sel(d_x_nop));
  Multiplexer #(.width(32), .enable("false")) multiplexer_8 (
    .in0(n32_bit_compact_2_result), .in1(d_x_ir), .out(br_address), .sel(d_x_bex));
  Multiplexer #(.width(32), .enable("false")) multiplexer_9 (
    .in0(d_x_ir), .in1(D_X_B_output), .out(d_x_j_address), .sel(d_x_jr));
  r_decoder r_decoder_1 (
    .alu_opcode(alu_op), .add(d_x_add), .sub(d_x_sub), .\and (d_x_and), .\or (d_x_or), .sll(d_x_sll),
    .sra(d_x_sa));
  _32_bit_compact u_32_bit_compact_2 (
    .result(n32_bit_compact_2_result), .A(D_X_PC_output), .B(bit_extender_2_out), .sub(1'b0));  // open: ovf
  register_32 D_X_PC (.clk(clk), .\input (F_D_PC_output), .enable(1'b1), .\output (D_X_PC_output), .reset(reset));
  register_32 D_X_A (
    .clk(clk), .\input (RegisterFile_readdata1), .enable(1'b1), .\output (D_X_A_output), .reset(reset));
  register_32 D_X_B (
    .clk(clk), .\input (RegisterFile_readdata2), .enable(1'b1), .\output (D_X_B_output), .reset(reset));
  register_32 u_D_X_IR (.clk(clk), .\input (multiplexer_7_out), .enable(1'b1), .\output (d_x_ir), .reset(reset));
  // Probe on d_x_ir
  or or_7 (or_7_out, d_x_addi, d_x_sub, d_x_add);
  and and_10 (overflow, or_7_out, alu_ovf);
  or or_8 (d_x_j____jal____jr, d_x_jr, d_x_jal, d_x_j);
  _5_bit_equal u_5_bit_equal_7 (.A(d_x_rs1), .B({5{1'b0}}), .isEqual(d_x_rs1_____r0));
  _5_bit_equal u_5_bit_equal_8 (.A(d_x_rs2), .B({5{1'b0}}), .isEqual(d_x_rs2_____r0));
  assign bit_extender_2_out = {{15{d_x_ir[16]}}, d_x_ir[16:0]};  // Bit_Extender bit_extender_2
  decoder decoder_2 (
    .opcode(d_x_ir[31:27]), .r(d_x_r), .addi(d_x_addi), .sw(d_x_sw), .lw(d_x_lw), .j(d_x_j), .bne(d_x_bne),
    .jal(d_x_jal), .jr(d_x_jr), .blt(d_x_blt), .bex(d_x_bex), .setx(d_x_setx), .swtp(d_x_swtp),
    .swtc(d_x_swtc), .\rand (d_x_rand));
  Multiplexer #(.width(5), .enable("false")) multiplexer_10 (
    .in0(alu_op), .in1(multiplexer_11_out), .out(alu_op_in), .sel(not_10_out));
  Multiplexer #(.width(5), .enable("false")) multiplexer_11 (
    .in0({5{1'b0}}), .in1(5'b00001), .out(multiplexer_11_out), .sel(need_subtraction));
  not not_10 (not_10_out, d_x_r);
  or or_9 (need_subtraction, d_x_bne, d_x_blt, d_x_bex);
  Multiplexer #(.width(32), .enable("false")) multiplexer_12 (
    .in0(D_X_A_output), .in1({x_m_o, module_addr}), .out(multiplexer_12_out), .sel(d_x_rs1____x_m_rd));
  Multiplexer #(.width(32), .enable("false")) multiplexer_13 (
    .in0(D_X_B_output), .in1({x_m_o, module_addr}), .out(multiplexer_13_out), .sel(d_x_rs2____x_m_rd));
  or or_10 (d_x_rd_rt, d_x_bne, d_x_blt, d_x_swtp, d_x_jr, d_x_sw, d_x_swtc);
  Multiplexer #(.width(32), .enable("false")) multiplexer_14 (
    .in0(multiplexer_12_out), .in1(rf_wdata), .out(multiplexer_14_out), .sel(d_x_rs1____m_w_rd));
  Multiplexer #(.width(32), .enable("false")) multiplexer_15 (
    .in0(multiplexer_13_out), .in1(rf_wdata), .out(multiplexer_15_out), .sel(d_x_rs2____m_w_rd));
  Multiplexer #(.width(32), .enable("false")) multiplexer_16 (
    .in0(32'ha8000001), .in1(multiplexer_17_out), .out(multiplexer_16_out), .sel(d_x_addi));
  Multiplexer #(.width(32), .enable("false")) multiplexer_17 (
    .in0(32'ha8000002), .in1(32'ha8000003), .out(multiplexer_17_out), .sel(d_x_sub));
  _5_bit_equal u_5_bit_equal_9 (.A(d_x_rs1), .B(rstatus[26:22]), .isEqual(n5_bit_equal_9_isequal));
  _5_bit_equal u_5_bit_equal_10 (.A(d_x_rs1), .B(m_w_ir[26:22]), .isEqual(n5_bit_equal_10_isequal));
  _5_bit_equal u_5_bit_equal_11 (.A(d_x_rs2), .B(m_w_ir[26:22]), .isEqual(n5_bit_equal_11_isequal));
  _5_bit_equal u_5_bit_equal_12 (.A(d_x_rs2), .B(rstatus[26:22]), .isEqual(n5_bit_equal_12_isequal));
  Multiplexer #(.width(32), .enable("false")) multiplexer_18 (
    .in0(multiplexer_19_out), .in1(bit_extender_3_out), .out(multiplexer_18_out), .sel(bex_m_x_bypass));
  Multiplexer #(.width(32), .enable("false")) multiplexer_19 (
    .in0(multiplexer_15_out), .in1(bit_extender_2_out), .out(multiplexer_19_out), .sel(d_x_N____B));
  Multiplexer #(.width(32), .enable("false")) multiplexer_20 (
    .in0(d_x_ir), .in1(multiplexer_16_out),
    .out({multiplexer_20_out[31:12], multiplexer_20_out_2, alu_op, multiplexer_20_out[1:0]}), .sel(overflow));
  ALU alu_1 (
    .InputData1(multiplexer_14_out), .ALUop(alu_op_in), .InputData2(multiplexer_18_out), .out_8(alu_1_out_8),
    .shift(multiplexer_20_out_2), .ovf(alu_ovf), .BLT(alu_lt), .BNE(alu_ne));
  assign bit_extender_3_out = {{5{1'b0}}, rstatus};  // Bit_Extender bit_extender_3
  Multiplexer #(.width(5), .enable("false")) multiplexer_21 (
    .in0(d_x_ir[16:12]), .in1(d_x_ir[26:22]), .out(multiplexer_21_out), .sel(d_x_rd_rt));
  not not_11 (not_11_out, d_x_rs1_____r0);
  not not_12 (not_12_out, d_x_rs2_____r0);
  or or_11 (d_x_N____B, d_x_swtp, d_x_swtc, d_x_lw, d_x_sw, d_x_addi);
  Multiplexer #(.width(5), .enable("false")) multiplexer_22 (
    .in0(d_x_ir[21:17]), .in1({5{1'b0}}), .out(d_x_rs1), .sel(d_x_bex));
  Multiplexer #(.width(5), .enable("false")) multiplexer_23 (
    .in0(multiplexer_21_out), .in1(5'b11110), .out(d_x_rs2), .sel(d_x_bex));
  and and_11 (d_x_rs1____x_m_rd, n5_bit_equal_9_isequal, x_m_writes, not_11_out);
  and and_12 (d_x_rs1____m_w_rd, n5_bit_equal_10_isequal, m_w_writes, not_11_out);
  and and_13 (d_x_rs2____m_w_rd, n5_bit_equal_11_isequal, m_w_writes, not_12_out);
  and and_14 (d_x_rs2____x_m_rd, n5_bit_equal_12_isequal, x_m_writes, not_12_out);
  or or_12 (d_x_writes, d_x_r, d_x_addi, d_x_lw, d_x_jal, d_x_setx, d_x_rand);
  Random #(.width(32)) random_1 (.clk(clk), .next(1'b1), .out(random_1_out));  // open: clr
  Multiplexer #(.width(32), .enable("false")) multiplexer_24 (
    .in0(alu_1_out_8), .in1(D_X_PC_output), .out(multiplexer_24_out), .sel(d_x_jal));
  Multiplexer #(.width(32), .enable("false")) multiplexer_25 (
    .in0(multiplexer_24_out), .in1(random_1_out), .out(multiplexer_25_out), .sel(d_x_rand));
  // Probe on {x_m_o, module_addr}
  register_32 u_X_M_O (
    .clk(clk), .\input (multiplexer_25_out), .enable(1'b1), .\output ({x_m_o, module_addr}), .reset(reset));
  register_32 X_M_B (.clk(clk), .\input (multiplexer_15_out), .enable(1'b1), .\output (X_M_B_output), .reset(reset));
  register_32 u_X_M_IR (
    .clk(clk), .\input ({multiplexer_20_out[31:12], multiplexer_20_out_2, alu_op, multiplexer_20_out[1:0]}),
    .enable(1'b1), .\output ({x_m_ir, rstatus}), .reset(reset));
  decoder decoder_3 (
    .opcode(x_m_ir), .r(x_m_r), .addi(x_m_addi), .sw(x_m_sw), .lw(x_m_lw), .j(x_m_j), .bne(x_m_bne),
    .jal(x_m_jal), .jr(x_m_jr), .blt(x_m_blt), .bex(x_m_bex), .setx(x_m_setx), .swtp(x_m_swtp),
    .swtc(x_m_swtc), .\rand (x_m_rand));
  or or_13 (x_m_rd_rt, x_m_bne, x_m_blt, x_m_swtp, x_m_jr, x_m_sw, x_m_swtc);
  and and_15 (bex_m_x_bypass, x_m_setx, d_x_bex);
  Multiplexer #(.width(32), .enable("false")) multiplexer_26 (
    .in0(X_M_B_output), .in1(rf_wdata), .out(module_data), .sel(x_m_rs2____m_w_rd));
  _5_bit_equal u_5_bit_equal_13 (.A(x_m_rs2), .B(m_w_ir[26:22]), .isEqual(n5_bit_equal_13_isequal));
  and and_16 (x_m_rs2____m_w_rd, n5_bit_equal_13_isequal, not_13_out);
  not not_13 (not_13_out, x_m_rs2_____r0);
  _5_bit_equal u_5_bit_equal_14 (.A(x_m_rs2), .B({5{1'b0}}), .isEqual(x_m_rs2_____r0));
  Multiplexer #(.width(5), .enable("false")) multiplexer_27 (
    .in0(rstatus[16:12]), .in1(rstatus[26:22]), .out(x_m_rs2), .sel(x_m_rd_rt));
  or or_14 (x_m_writes, x_m_r, x_m_addi, x_m_lw, x_m_jal, x_m_setx, x_m_rand);
  RAM #(.addrWidth(12), .dataWidth(32), .bus("separate")) ram_1 (
    .addr({x_m_o[11:4], module_addr}), .din(module_data), .data(ram_1_data), .str(x_m_sw), .clk(clk));  // open: sel, ld, clr
  register_32 M_W_O (.clk(clk), .\input ({x_m_o, module_addr}), .enable(1'b1), .\output (M_W_O_output), .reset(reset));
  register_32 M_W_D (.clk(clk), .\input (ram_1_data), .enable(1'b1), .\output (M_W_D_output), .reset(reset));
  register_32 u_M_W_IR (.clk(clk), .\input ({x_m_ir, rstatus}), .enable(1'b1), .\output (m_w_ir), .reset(reset));
  Multiplexer #(.width(32), .enable("false")) multiplexer_28 (
    .in0(M_W_O_output), .in1(bit_extender_4_out), .out(multiplexer_28_out), .sel(m_w_setx));
  assign bit_extender_4_out = {{5{1'b0}}, m_w_ir[26:0]};  // Bit_Extender bit_extender_4
  Multiplexer #(.width(5), .enable("false")) multiplexer_29 (
    .in0(m_w_ir[26:22]), .in1(5'b11110), .out(multiplexer_29_out), .sel(m_w_setx));
  decoder decoder_4 (
    .opcode(m_w_ir[31:27]), .r(m_w_r), .addi(m_w_addi), .sw(m_w_sw), .lw(m_w_lw), .j(m_w_j), .bne(m_w_bne),
    .jal(m_w_jal), .jr(m_w_jr), .blt(m_w_blt), .bex(m_w_bex), .setx(m_w_setx), .swtp(m_w_swtp),
    .swtc(m_w_swtc), .\rand (m_w_rand));
  Multiplexer #(.width(32), .enable("false")) multiplexer_30 (
    .in0(multiplexer_28_out), .in1(M_W_D_output), .out(rf_wdata), .sel(m_w_lw));
  Multiplexer #(.width(5), .enable("false")) multiplexer_31 (
    .in0(multiplexer_29_out), .in1({5{1'b1}}), .out(rf_wreg), .sel(m_w_jal));
  // Probe on m_w_ir
  or or_15 (m_w_writes, m_w_r, m_w_addi, m_w_lw, m_w_jal, m_w_setx, m_w_rand);

  // Other names for the same wires on the sheet: d_x_rt[4:0] = d_x_ir[16:12]; d_x_rs[4:0] = d_x_ir[21:17];
  //   d_x_rd[4:0] = d_x_ir[26:22]; f_d_rt[4:0] = f_d_ir[16:12]; f_d_rs[4:0] = f_d_ir[21:17];
  //   f_d_rd[4:0] = f_d_ir[26:22]; m_w_rt[4:0] = m_w_ir[16:12]; m_w_rs[4:0] = m_w_ir[21:17];
  //   m_w_rd[4:0] = m_w_ir[26:22]; rf_we = m_w_writes; x_m_ir[26:0] = rstatus; x_m_rt[4:0] = rstatus[16:12];
  //   x_m_rs[4:0] = rstatus[21:17]; x_m_rs1[4:0] = rstatus[21:17]; x_m_rd[4:0] = rstatus[26:22];
  //   x_m_o[3:0] = module_addr

  // Notes on the sheet:
  //   contents of rom_1 (hex, n*v repeats v):
  //   400000 800000 c00000 1000000 1400000 28800010 40c20000 d0c20000 28420001 3045fffc d9000000 c1000000
  //   1041ffff
  //   FETCH
  //   STALL FOR LW/SW HAZARD
  //   FLUSH FOR JUMP
  //   F/D IR DECODER
  //   BRANCH LOGIC
  //   DATA HAZARD DETECTION
  //   not gate in front of alu lt because A and B are switched
  //   DECODE
  //   CHOOSING RS1 & RS2
  //   to avoid passing for no-ops
  //   D/X IR DECODER
  //   ALU OP DECODE
  //   only overflow if add, addi or sub
  //   JUMP
  //   to avoid passing for no-ops
  //   SET ALU OP INPUT
  //   ALU op in must be subtraction in branch ir's
  //   EXECUTE
  //   CHOOSING RS1 & RS2
  //   DATA HAZARD DETECTION
  //   DOES D/X IR WRITE?
  //   USE N AS ALU INPUT B?
  //   X/M IR DECODER
  //   MEMORY
  //   Goes to memory module (MM)
  //   CHOOSING RS1 & RS2
  //   DATA HAZARD DETECTION
  //   to avoid passing for no-ops
  //   DOES X/M IR WRITE?
  //   WRITEBACK
  //   M/W IR DECODER
  //   DOES W/M IR WRITE?
endmodule

module card_matching (
  input  clk,
  input  [3:0] in_2,
  input  reset,
  input  [3:0] in_4,
  input  wr_en,
  input  [15:0] \time ,
  output Solved
);

  wire _0_cards_selected, _1_card_selected, _2_cards_equal, _2_cards_incorrect, _2_cards_matched,
       _2_cards_selected, and_1_out, and_2_out, button_pressed, c0_btn, c0_solved, c0_solved_1, c0_solved_2,
       c1_btn, c1_btn_t, c1_solved, c1_solved_1, c1_solved_2, c2_btn, c2_btn_t, c2_solved, c2_solved_1,
       c2_solved_2, c3_btn, c3_btn_t, c3_solved, c3_solved_1, c3_solved_2, c4_btn, c4_btn_t, c4_solved,
       c4_solved_1, c4_solved_2, c5_btn, c5_btn_t, c5_solved, c5_solved_1, c5_solved_2, c6_btn, c6_btn_t,
       c6_solved, c6_solved_1, c6_solved_2, c7_btn, c7_btn_t, c7_solved, c7_solved_1, c7_solved_2, c8_btn,
       c8_btn_t, c8_solved, c8_solved_1, c8_solved_2, c9_btn, c9_btn_t, c9_solved, c9_solved_1, c9_solved_2,
       c10_btn, c10_btn_t, c10_solved, c10_solved_1, c10_solved_2, c11_btn, c11_btn_t, c11_solved,
       c11_solved_1, c11_solved_2, c12_btn, c12_btn_t, c12_solved, c12_solved_1, c12_solved_2, c13_btn,
       c13_btn_t, c13_solved, c13_solved_1, c13_solved_2, c14_btn, c14_btn_t, c14_solved, c14_solved_1,
       c14_solved_2, c15_btn, c15_btn_t, c15_solved, c15_solved_1, c15_solved_2, card_1____card_2,
       decoder_1_out0, decoder_1_out1, decoder_1_out2, decoder_1_out3, decoder_1_out4, decoder_1_out5,
       decoder_1_out6, decoder_1_out7, decoder_1_out8, decoder_1_out9, decoder_1_out10, decoder_1_out11,
       decoder_1_out12, decoder_1_out13, decoder_1_out14, decoder_1_out15, decoder_2_out0, decoder_2_out1,
       decoder_2_out2, decoder_2_out3, decoder_2_out4, decoder_2_out5, decoder_2_out6, decoder_2_out7,
       decoder_2_out8, decoder_2_out9, decoder_2_out10, decoder_2_out11, decoder_2_out12, decoder_2_out13,
       decoder_2_out14, decoder_2_out15, en0, en1, en2, en3, en4, en5, en6, en7, en8, en9, en10, en11, en12,
       en13, en14, en15, facedown, n4_bit_equal_1_isequal, not_1_out, not_2_out, not_3_out, not_4_out,
       not_5_out, not_6_out, not_7_out, not_8_out, not_9_out, not_10_out, not_11_out, not_12_out, not_13_out,
       not_14_out, not_15_out, not_16_out, not_18_out, or_1_out, or_3_out, or_4_out, or_5_out, or_6_out,
       or_7_out, or_8_out, or_9_out, or_10_out, or_11_out, or_12_out, or_13_out, or_14_out, or_15_out,
       or_16_out, or_17_out, or_18_out;
  wire [1:0] c0_state, c1_state, c2_state, c3_state, c4_state, c5_state, c6_state, c7_state, c8_state,
       c9_state, c10_state, c11_state, c12_state, c13_state, c14_state, c15_state, cards_sel;
  wire [3:0] btn_id_16_1_out, c0, c0_in, c1, c1_in, c2, c2_in, c3, c3_in, c4, c4_in, c5, c5_in, c6, c6_in,
       c7, c7_in, c8, c8_in, c9, c9_in, c10, c10_in, c11, c11_in, c12, c12_in, c13, c13_in, c14, c14_in, c15,
       c15_in, card_1_value, card_2_value, selected_card, selected_card_1, selected_card_2;
  wire [31:0] bit_extender_1_out;
  wire [31:4] register_32_1_output, register_32_2_output, register_32_3_output, register_32_4_output,
       register_32_5_output, register_32_6_output, register_32_7_output, register_32_8_output,
       register_32_9_output, register_32_10_output, register_32_11_output, register_32_12_output,
       register_32_13_output, register_32_14_output, register_32_15_output, register_32_16_output;

  Button button_1 (.out(c0_btn));
  Button button_2 (.out(c4_btn_t));
  Button button_3 (.out(c8_btn_t));
  Button button_4 (.out(c12_btn_t));
  LED led_1 (.in(c0_state[1]));
  Hex_Digit_Display hex_digit_display_1 (.value(c0_in));  // open: dp
  LED led_2 (.in(c4_state[1]));
  Hex_Digit_Display hex_digit_display_2 (.value(c4_in));  // open: dp
  LED led_3 (.in(c8_state[1]));
  Hex_Digit_Display hex_digit_display_3 (.value(c8_in));  // open: dp
  LED led_4 (.in(c12_state[1]));
  Hex_Digit_Display hex_digit_display_4 (.value(c12_in));  // open: dp
  LED led_5 (.in(c1_state[1]));
  Button button_5 (.out(c1_btn_t));
  Hex_Digit_Display hex_digit_display_5 (.value(c1_in));  // open: dp
  LED led_6 (.in(c5_state[1]));
  Button button_6 (.out(c5_btn_t));
  Hex_Digit_Display hex_digit_display_6 (.value(c5_in));  // open: dp
  LED led_7 (.in(c9_state[1]));
  Button button_7 (.out(c9_btn_t));
  Hex_Digit_Display hex_digit_display_7 (.value(c9_in));  // open: dp
  LED led_8 (.in(c13_state[1]));
  Button button_8 (.out(c13_btn_t));
  Hex_Digit_Display hex_digit_display_8 (.value(c13_in));  // open: dp
  Hex_Digit_Display hex_digit_display_9 (.value(btn_id_16_1_out));  // open: dp
  btn_id_16 btn_id_16_1 (
    .c0(c0_btn), .c1(c1_btn), .c2(c2_btn), .c3(c3_btn), .c4(c4_btn), .c5(c5_btn), .c6(c6_btn), .c7(c7_btn),
    .c8(c8_btn), .c9(c9_btn), .c10(c10_btn), .c11(c11_btn), .c12(c12_btn), .c13(c13_btn), .c14(c14_btn),
    .c15(c15_btn), .out(btn_id_16_1_out), .btn_pressed(button_pressed));
  Hex_Digit_Display hex_digit_display_10 (.value(\time [15:12]));  // open: dp
  Button button_9 (.out(c2_btn_t));
  Button button_10 (.out(c6_btn_t));
  Button button_11 (.out(c10_btn_t));
  Button button_12 (.out(c14_btn_t));
  Register #(.width(4)) selected_reg_1 (
    .D(btn_id_16_1_out), .en(1'b1), .Q(selected_card), .clk(button_pressed), .clr(reset));
  Hex_Digit_Display hex_digit_display_11 (.value(\time [11:8]), .dp(1'b1));
  LED led_9 (.in(c2_state[1]));
  Hex_Digit_Display hex_digit_display_12 (.value(c2_in));  // open: dp
  LED led_10 (.in(c6_state[1]));
  Hex_Digit_Display hex_digit_display_13 (.value(c6_in));  // open: dp
  LED led_11 (.in(c10_state[1]));
  Hex_Digit_Display hex_digit_display_14 (.value(c10_in));  // open: dp
  LED led_12 (.in(c14_state[1]));
  Hex_Digit_Display hex_digit_display_15 (.value(c14_in));  // open: dp
  Hex_Digit_Display hex_digit_display_16 (.value(\time [3:0]));  // open: dp
  Hex_Digit_Display hex_digit_display_17 (.value(\time [7:4]));  // open: dp
  LED led_13 (.in(c3_state[1]));
  Button button_13 (.out(c3_btn_t));
  Hex_Digit_Display hex_digit_display_18 (.value(c3_in));  // open: dp
  LED led_14 (.in(c7_state[1]));
  Button button_14 (.out(c7_btn_t));
  Hex_Digit_Display hex_digit_display_19 (.value(c7_in));  // open: dp
  LED led_15 (.in(c11_state[1]));
  Button button_15 (.out(c11_btn_t));
  Hex_Digit_Display hex_digit_display_20 (.value(c11_in));  // open: dp
  LED led_16 (.in(c15_state[1]));
  Button button_16 (.out(c15_btn_t));
  Hex_Digit_Display hex_digit_display_21 (.value(c15_in));  // open: dp
  and and_1 (and_1_out, card_1____card_2, _1_card_selected);
  assign bit_extender_1_out = {{28{1'b0}}, in_4};  // Bit_Extender bit_extender_1
  and and_2 (and_2_out, _1_card_selected, card_1____card_2);
  or or_1 (or_1_out, _0_cards_selected, and_1_out);
  _4_bit_equal u_4_bit_equal_1 (.A(selected_card), .B(selected_card_1), .isEqual(n4_bit_equal_1_isequal));
  not not_1 (not_1_out, clk);
  not not_2 (not_2_out, clk);
  not not_3 (not_3_out, clk);
  not not_4 (not_4_out, clk);
  not not_5 (not_5_out, clk);
  not not_6 (not_6_out, clk);
  not not_7 (not_7_out, clk);
  not not_8 (not_8_out, clk);
  not not_9 (not_9_out, clk);
  not not_10 (not_10_out, clk);
  not not_11 (not_11_out, clk);
  not not_12 (not_12_out, clk);
  not not_13 (not_13_out, clk);
  not not_14 (not_14_out, clk);
  not not_15 (not_15_out, clk);
  not not_16 (not_16_out, clk);
  Register #(.width(4), .trigger("falling")) selected_reg_1_2 (
    .D(selected_card), .en(_0_cards_selected), .Q(selected_card_1), .clk(button_pressed), .clr(facedown));
  Register #(.width(4), .trigger("falling")) selected_reg_2 (
    .D(selected_card), .en(and_2_out), .Q(selected_card_2), .clk(button_pressed), .clr(facedown));
  // Probe on cards_sel
  Counter #(.width(2), .max('h3)) u_cards_sel (
    .D(cards_sel), .count(or_1_out), .Q(cards_sel), .clk(button_pressed), .clr(facedown));  // open: load, carry
  not not_17 (card_1____card_2, n4_bit_equal_1_isequal);
  register_32 register_32_1 (
    .clk(not_1_out), .\input (bit_extender_1_out), .enable(en0), .\output ({register_32_1_output, c0}),
    .reset(reset));
  register_32 register_32_2 (
    .clk(not_2_out), .\input (bit_extender_1_out), .enable(en1), .\output ({register_32_2_output, c1}),
    .reset(reset));
  register_32 register_32_3 (
    .clk(not_3_out), .\input (bit_extender_1_out), .enable(en2), .\output ({register_32_3_output, c2}),
    .reset(reset));
  register_32 register_32_4 (
    .clk(not_4_out), .\input (bit_extender_1_out), .enable(en3), .\output ({register_32_4_output, c3}),
    .reset(reset));
  register_32 register_32_5 (
    .clk(not_5_out), .\input (bit_extender_1_out), .enable(en4), .\output ({register_32_5_output, c4}),
    .reset(reset));
  register_32 register_32_6 (
    .clk(not_6_out), .\input (bit_extender_1_out), .enable(en5), .\output ({register_32_6_output, c5}),
    .reset(reset));
  register_32 register_32_7 (
    .clk(not_7_out), .\input (bit_extender_1_out), .enable(en6), .\output ({register_32_7_output, c6}),
    .reset(reset));
  register_32 register_32_8 (
    .clk(not_8_out), .\input (bit_extender_1_out), .enable(en7), .\output ({register_32_8_output, c7}),
    .reset(reset));
  register_32 register_32_9 (
    .clk(not_9_out), .\input (bit_extender_1_out), .enable(en8), .\output ({register_32_9_output, c8}),
    .reset(reset));
  register_32 register_32_10 (
    .clk(not_10_out), .\input (bit_extender_1_out), .enable(en9), .\output ({register_32_10_output, c9}),
    .reset(reset));
  register_32 register_32_11 (
    .clk(not_11_out), .\input (bit_extender_1_out), .enable(en10), .\output ({register_32_11_output, c10}),
    .reset(reset));
  register_32 register_32_12 (
    .clk(not_12_out), .\input (bit_extender_1_out), .enable(en11), .\output ({register_32_12_output, c11}),
    .reset(reset));
  register_32 register_32_13 (
    .clk(not_13_out), .\input (bit_extender_1_out), .enable(en12), .\output ({register_32_13_output, c12}),
    .reset(reset));
  register_32 register_32_14 (
    .clk(not_14_out), .\input (bit_extender_1_out), .enable(en13), .\output ({register_32_14_output, c13}),
    .reset(reset));
  register_32 register_32_15 (
    .clk(not_15_out), .\input (bit_extender_1_out), .enable(en14), .\output ({register_32_15_output, c14}),
    .reset(reset));
  register_32 register_32_16 (
    .clk(not_16_out), .\input (bit_extender_1_out), .enable(en15), .\output ({register_32_16_output, c15}),
    .reset(reset));
  Hex_Digit_Display hex_digit_display_22 (.value(selected_card_1));  // open: dp
  Hex_Digit_Display hex_digit_display_23 (.value(selected_card_2));  // open: dp
  card_state card_state_1 (.card_btn(c0_btn), .card_solved(c0_solved), .card_state(c0_state), .reset(facedown));
  card_state card_state_2 (.card_btn(c1_btn_t), .card_solved(c1_solved), .card_state(c1_state), .reset(facedown));
  card_state card_state_3 (.card_btn(c2_btn_t), .card_solved(c2_solved), .card_state(c2_state), .reset(facedown));
  card_state card_state_4 (.card_btn(c3_btn_t), .card_solved(c3_solved), .card_state(c3_state), .reset(facedown));
  card_state card_state_5 (.card_btn(c4_btn_t), .card_solved(c4_solved), .card_state(c4_state), .reset(facedown));
  card_state card_state_6 (.card_btn(c5_btn_t), .card_solved(c5_solved), .card_state(c5_state), .reset(facedown));
  card_state card_state_7 (.card_btn(c6_btn_t), .card_solved(c6_solved), .card_state(c6_state), .reset(facedown));
  card_state card_state_8 (.card_btn(c7_btn_t), .card_solved(c7_solved), .card_state(c7_state), .reset(facedown));
  not not_18 (not_18_out, _2_cards_equal);
  _2_bit_equal u_2_bit_equal_1 (.A(cards_sel), .B(2'b00), .isEqual(_0_cards_selected));
  _2_bit_equal u_2_bit_equal_2 (.A(cards_sel), .B(2'b01), .isEqual(_1_card_selected));
  _2_bit_equal u_2_bit_equal_3 (.A(cards_sel), .B(2'b10), .isEqual(_2_cards_selected));
  _4_bit_equal u_4_bit_equal_2 (.A(card_1_value), .B(card_2_value), .isEqual(_2_cards_equal));
  and and_3 (_2_cards_incorrect, not_18_out, _2_cards_selected);
  and and_4 (_2_cards_matched, _2_cards_selected, _2_cards_equal);
  or or_2 (facedown, _2_cards_selected, reset);
  card_state card_state_9 (.card_btn(c8_btn_t), .card_solved(c8_solved), .card_state(c8_state), .reset(facedown));
  card_state card_state_10 (.card_btn(c9_btn_t), .card_solved(c9_solved), .card_state(c9_state), .reset(facedown));
  card_state card_state_11 (.card_btn(c10_btn_t), .card_solved(c10_solved), .card_state(c10_state), .reset(facedown));
  card_state card_state_12 (.card_btn(c11_btn_t), .card_solved(c11_solved), .card_state(c11_state), .reset(facedown));
  card_state card_state_13 (.card_btn(c12_btn_t), .card_solved(c12_solved), .card_state(c12_state), .reset(facedown));
  card_state card_state_14 (.card_btn(c13_btn_t), .card_solved(c13_solved), .card_state(c13_state), .reset(facedown));
  card_state card_state_15 (.card_btn(c14_btn_t), .card_solved(c14_solved), .card_state(c14_state), .reset(facedown));
  card_state card_state_16 (.card_btn(c15_btn_t), .card_solved(c15_solved), .card_state(c15_state), .reset(facedown));
  assign c0_in = c0_state[0] ? c0 : 4'bz;  // Controlled_Buffer controlled_buffer_1
  assign c1_in = c1_state[0] ? c1 : 4'bz;  // Controlled_Buffer controlled_buffer_2
  assign c2_in = c2_state[0] ? c2 : 4'bz;  // Controlled_Buffer controlled_buffer_3
  assign c3_in = c3_state[0] ? c3 : 4'bz;  // Controlled_Buffer controlled_buffer_4
  assign c4_in = c4_state[0] ? c4 : 4'bz;  // Controlled_Buffer controlled_buffer_5
  assign c5_in = c5_state[0] ? c5 : 4'bz;  // Controlled_Buffer controlled_buffer_6
  assign c6_in = c6_state[0] ? c6 : 4'bz;  // Controlled_Buffer controlled_buffer_7
  assign c7_in = c7_state[0] ? c7 : 4'bz;  // Controlled_Buffer controlled_buffer_8
  assign c8_in = c8_state[0] ? c8 : 4'bz;  // Controlled_Buffer controlled_buffer_9
  assign c9_in = c9_state[0] ? c9 : 4'bz;  // Controlled_Buffer controlled_buffer_10
  assign c10_in = c10_state[0] ? c10 : 4'bz;  // Controlled_Buffer controlled_buffer_11
  assign c11_in = c11_state[0] ? c11 : 4'bz;  // Controlled_Buffer controlled_buffer_12
  assign c12_in = c12_state[0] ? c12 : 4'bz;  // Controlled_Buffer controlled_buffer_13
  assign c13_in = c13_state[0] ? c13 : 4'bz;  // Controlled_Buffer controlled_buffer_14
  assign c14_in = c14_state[0] ? c14 : 4'bz;  // Controlled_Buffer controlled_buffer_15
  assign c15_in = c15_state[0] ? c15 : 4'bz;  // Controlled_Buffer controlled_buffer_16
  assign card_1_value = decoder_1_out1 ? c1 : 4'bz;  // Controlled_Buffer controlled_buffer_17
  assign card_1_value = decoder_1_out0 ? c0 : 4'bz;  // Controlled_Buffer controlled_buffer_18
  assign card_2_value = decoder_2_out1 ? c1 : 4'bz;  // Controlled_Buffer controlled_buffer_19
  assign card_2_value = decoder_2_out0 ? c0 : 4'bz;  // Controlled_Buffer controlled_buffer_20
  assign card_1_value = decoder_1_out2 ? c2 : 4'bz;  // Controlled_Buffer controlled_buffer_21
  assign card_2_value = decoder_2_out2 ? c2 : 4'bz;  // Controlled_Buffer controlled_buffer_22
  Demultiplexer #(.select(4), .disabled(0)) demultiplexer_1 (
    .out0(c0_solved_1), .out1(c1_solved_1), .out2(c2_solved_1), .out3(c3_solved_1), .out4(c4_solved_1),
    .out5(c5_solved_1), .out6(c6_solved_1), .out7(c7_solved_1), .out8(c8_solved_1), .out9(c9_solved_1),
    .out10(c10_solved_1), .out11(c11_solved_1), .out12(c12_solved_1), .out13(c13_solved_1),
    .out14(c14_solved_1), .out15(c15_solved_1), .in(1'b1), .sel(selected_card_1), .en(_2_cards_matched));
  Demultiplexer #(.select(4), .disabled(0)) demultiplexer_2 (
    .out0(c0_solved_2), .out1(c1_solved_2), .out2(c2_solved_2), .out3(c3_solved_2), .out4(c4_solved_2),
    .out5(c5_solved_2), .out6(c6_solved_2), .out7(c7_solved_2), .out8(c8_solved_2), .out9(c9_solved_2),
    .out10(c10_solved_2), .out11(c11_solved_2), .out12(c12_solved_2), .out13(c13_solved_2),
    .out14(c14_solved_2), .out15(c15_solved_2), .in(1'b1), .sel(selected_card_2), .en(_2_cards_matched));
  assign card_1_value = decoder_1_out4 ? c4 : 4'bz;  // Controlled_Buffer controlled_buffer_23
  assign card_1_value = decoder_1_out3 ? c3 : 4'bz;  // Controlled_Buffer controlled_buffer_24
  assign card_2_value = decoder_2_out3 ? c3 : 4'bz;  // Controlled_Buffer controlled_buffer_25
  assign card_2_value = decoder_2_out4 ? c4 : 4'bz;  // Controlled_Buffer controlled_buffer_26
  assign card_1_value = decoder_1_out6 ? c6 : 4'bz;  // Controlled_Buffer controlled_buffer_27
  assign card_1_value = decoder_1_out5 ? c5 : 4'bz;  // Controlled_Buffer controlled_buffer_28
  assign card_2_value = decoder_2_out5 ? c5 : 4'bz;  // Controlled_Buffer controlled_buffer_29
  assign card_1_value = decoder_1_out7 ? c7 : 4'bz;  // Controlled_Buffer controlled_buffer_30
  assign card_2_value = decoder_2_out6 ? c6 : 4'bz;  // Controlled_Buffer controlled_buffer_31
  assign card_2_value = decoder_2_out7 ? c7 : 4'bz;  // Controlled_Buffer controlled_buffer_32
  assign card_1_value = decoder_1_out9 ? c9 : 4'bz;  // Controlled_Buffer controlled_buffer_33
  assign card_1_value = decoder_1_out8 ? c8 : 4'bz;  // Controlled_Buffer controlled_buffer_34
  assign card_2_value = decoder_2_out9 ? c9 : 4'bz;  // Controlled_Buffer controlled_buffer_35
  assign card_2_value = decoder_2_out8 ? c8 : 4'bz;  // Controlled_Buffer controlled_buffer_36
  or or_3 (or_3_out, c0_solved_1, c0_solved_2);
  or or_4 (or_4_out, c1_solved_1, c1_solved_2);
  or or_5 (or_5_out, c2_solved_1, c2_solved_2);
  or or_6 (or_6_out, c3_solved_1, c3_solved_2);
  or or_7 (or_7_out, c4_solved_1, c4_solved_2);
  or or_8 (or_8_out, c5_solved_1, c5_solved_2);
  or or_9 (or_9_out, c6_solved_1, c6_solved_2);
  or or_10 (or_10_out, c7_solved_1, c7_solved_2);
  or or_11 (or_11_out, c8_solved_1, c8_solved_2);
  or or_12 (or_12_out, c9_solved_1, c9_solved_2);
  or or_13 (or_13_out, c10_solved_1, c10_solved_2);
  or or_14 (or_14_out, c11_solved_1, c11_solved_2);
  or or_15 (or_15_out, c12_solved_1, c12_solved_2);
  or or_16 (or_16_out, c13_solved_1, c13_solved_2);
  or or_17 (or_17_out, c14_solved_1, c14_solved_2);
  or or_18 (or_18_out, c15_solved_1, c15_solved_2);
  assign card_1_value = decoder_1_out10 ? c10 : 4'bz;  // Controlled_Buffer controlled_buffer_37
  assign card_2_value = decoder_2_out10 ? c10 : 4'bz;  // Controlled_Buffer controlled_buffer_38
  D_Flip_Flop #(.trigger("high")) d_ff_1 (
    .clk(or_3_out), .D(or_3_out), .Q(c0_solved), .en(or_3_out), .reset(reset));  // open: Qn, preset
  D_Flip_Flop #(.trigger("high")) d_ff_2 (
    .clk(or_4_out), .D(or_4_out), .Q(c1_solved), .en(or_4_out), .reset(reset));  // open: Qn, preset
  D_Flip_Flop #(.trigger("high")) d_ff_3 (
    .clk(or_5_out), .D(or_5_out), .Q(c2_solved), .en(or_5_out), .reset(reset));  // open: Qn, preset
  D_Flip_Flop #(.trigger("high")) d_ff_4 (
    .clk(or_6_out), .D(or_6_out), .Q(c3_solved), .en(or_6_out), .reset(reset));  // open: Qn, preset
  D_Flip_Flop #(.trigger("high")) d_ff_5 (
    .clk(or_7_out), .D(or_7_out), .Q(c4_solved), .en(or_7_out), .reset(reset));  // open: Qn, preset
  D_Flip_Flop #(.trigger("high")) d_ff_6 (
    .clk(or_8_out), .D(or_8_out), .Q(c5_solved), .en(or_8_out), .reset(reset));  // open: Qn, preset
  D_Flip_Flop #(.trigger("high")) d_ff_7 (
    .clk(or_9_out), .D(or_9_out), .Q(c6_solved), .en(or_9_out), .reset(reset));  // open: Qn, preset
  D_Flip_Flop #(.trigger("high")) d_ff_8 (
    .clk(or_10_out), .D(or_10_out), .Q(c7_solved), .en(or_10_out), .reset(reset));  // open: Qn, preset
  D_Flip_Flop #(.trigger("high")) d_ff_9 (
    .clk(or_11_out), .D(or_11_out), .Q(c8_solved), .en(or_11_out), .reset(reset));  // open: Qn, preset
  D_Flip_Flop #(.trigger("high")) d_ff_10 (
    .clk(or_12_out), .D(or_12_out), .Q(c9_solved), .en(or_12_out), .reset(reset));  // open: Qn, preset
  D_Flip_Flop #(.trigger("high")) d_ff_11 (
    .clk(or_13_out), .D(or_13_out), .Q(c10_solved), .en(or_13_out), .reset(reset));  // open: Qn, preset
  D_Flip_Flop #(.trigger("high")) d_ff_12 (
    .clk(or_14_out), .D(or_14_out), .Q(c11_solved), .en(or_14_out), .reset(reset));  // open: Qn, preset
  D_Flip_Flop #(.trigger("high")) d_ff_13 (
    .clk(or_15_out), .D(or_15_out), .Q(c12_solved), .en(or_15_out), .reset(reset));  // open: Qn, preset
  D_Flip_Flop #(.trigger("high")) d_ff_14 (
    .clk(or_16_out), .D(or_16_out), .Q(c13_solved), .en(or_16_out), .reset(reset));  // open: Qn, preset
  D_Flip_Flop #(.trigger("high")) d_ff_15 (
    .clk(or_17_out), .D(or_17_out), .Q(c14_solved), .en(or_17_out), .reset(reset));  // open: Qn, preset
  D_Flip_Flop #(.trigger("high")) d_ff_16 (
    .clk(or_18_out), .D(or_18_out), .Q(c15_solved), .en(or_18_out), .reset(reset));  // open: Qn, preset
  assign card_1_value = decoder_1_out11 ? c11 : 4'bz;  // Controlled_Buffer controlled_buffer_39
  assign card_1_value = decoder_1_out12 ? c12 : 4'bz;  // Controlled_Buffer controlled_buffer_40
  assign card_2_value = decoder_2_out11 ? c11 : 4'bz;  // Controlled_Buffer controlled_buffer_41
  assign card_2_value = decoder_2_out12 ? c12 : 4'bz;  // Controlled_Buffer controlled_buffer_42
  assign card_1_value = decoder_1_out13 ? c13 : 4'bz;  // Controlled_Buffer controlled_buffer_43
  assign card_1_value = decoder_1_out14 ? c14 : 4'bz;  // Controlled_Buffer controlled_buffer_44
  Decoder #(.select(4), .enable("false")) decoder_1 (
    .out0(decoder_1_out0), .out1(decoder_1_out1), .out2(decoder_1_out2), .out3(decoder_1_out3),
    .out4(decoder_1_out4), .out5(decoder_1_out5), .out6(decoder_1_out6), .out7(decoder_1_out7),
    .out8(decoder_1_out8), .out9(decoder_1_out9), .out10(decoder_1_out10), .out11(decoder_1_out11),
    .out12(decoder_1_out12), .out13(decoder_1_out13), .out14(decoder_1_out14), .out15(decoder_1_out15),
    .sel(selected_card_1));
  assign card_2_value = decoder_2_out13 ? c13 : 4'bz;  // Controlled_Buffer controlled_buffer_45
  Decoder #(.select(4), .enable("false")) decoder_2 (
    .out0(decoder_2_out0), .out1(decoder_2_out1), .out2(decoder_2_out2), .out3(decoder_2_out3),
    .out4(decoder_2_out4), .out5(decoder_2_out5), .out6(decoder_2_out6), .out7(decoder_2_out7),
    .out8(decoder_2_out8), .out9(decoder_2_out9), .out10(decoder_2_out10), .out11(decoder_2_out11),
    .out12(decoder_2_out12), .out13(decoder_2_out13), .out14(decoder_2_out14), .out15(decoder_2_out15),
    .sel(selected_card_2));
  assign card_1_value = decoder_1_out15 ? c15 : 4'bz;  // Controlled_Buffer controlled_buffer_46
  assign card_2_value = decoder_2_out15 ? c15 : 4'bz;  // Controlled_Buffer controlled_buffer_47
  assign card_2_value = decoder_2_out14 ? c14 : 4'bz;  // Controlled_Buffer controlled_buffer_48
  Decoder #(.select(4), .disabled(0)) decoder_3 (
    .out0(en0), .out1(en1), .out2(en2), .out3(en3), .out4(en4), .out5(en5), .out6(en6), .out7(en7),
    .out8(en8), .out9(en9), .out10(en10), .out11(en11), .out12(en12), .out13(en13), .out14(en14),
    .out15(en15), .sel(in_2), .en(wr_en));
  and and_5 (Solved, c0_state[1], c1_state[1], c2_state[1], c3_state[1], c4_state[1], c5_state[1], c6_state[1], c7_state[1], c8_state[1], c9_state[1], c10_state[1], c11_state[1], c12_state[1], c13_state[1], c14_state[1], c15_state[1]);

  // Other names for the same wires on the sheet: reset_card_1 = facedown; reset_card_2 = facedown;
  //   reset_card_counter = facedown; write = wr_en; write_data[3:0] = in_4; write_reg[3:0] = in_2

  // Notes on the sheet:
  //   To flip a card, press the button to the left of it.
  //   Flip cards until they have all been solved.
  //   HOW TO PLAY
  //   Flip two cards at a time. If they match, they are considered "solved".
  //   If a card has been solved, its corresponding LED will light up on the next click.
  //   identifying selected card
  //   storing selected cards
  //   Make sure card 1 has been assigned and is not same as card 2
  //   counting number of selected card
  //   card values
  //   card states
  //   state 0 - facedown
  //   state 1 - faceup
  //   state 2 - solved
  //   evaluating cards
  //   if no cards have been selected yet
  //   if 1 card has been selected
  //   if 2 card has been selected
  //   determine next steps
  //   display inputs
  //   cards solved
  //   determining selected cards' values
  //   output
endmodule

module pattern_memory (
  input  [31:0] data,
  input  [15:0] \time ,
  input  clk,
  input  wr_en,
  input  clr,
  output solved
);

  wire B0, B1, B2, B3, btn_pressed, digit_solved, digit_wrong, display_pattern, L0, L1, L2, L3, mode,
       module_solved, n2_bit_equal_1_isequal, n2_bit_equal_2_isequal, not_1_out, not_2_out, or_1_out,
       or_2_out, pattern_solved, selection_made;
  wire [1:0] current_digit, current_pattern, display_digit, display_value, expected, selected_btn;
  wire [2:2] current_pattern_q;
  wire [3:0] counter_1_q;
  wire [7:0] multiplexer_1_out;
  wire [31:0] register_1_q;

  Hex_Digit_Display hex_digit_display_1 (.value(\time [15:12]));  // open: dp
  Hex_Digit_Display hex_digit_display_2 (.value(\time [11:8]), .dp(1'b1));
  Button button_1 (.out(B3));
  LED led_1 (.in(L3));
  Button button_2 (.out(B2));
  Button button_3 (.out(display_pattern));
  Hex_Digit_Display hex_digit_display_3 (.value(\time [3:0]));  // open: dp
  Hex_Digit_Display hex_digit_display_4 (.value(\time [7:4]));  // open: dp
  Button button_4 (.out(B0));
  LED led_2 (.in(L0));
  LED led_3 (.in(L1));
  Button button_5 (.out(B1));
  LED led_4 (.in(L2));
  // Probe on current_pattern
  Counter #(.width(6), .max('h3f), .ongoal("stay")) counter_1 (
    .count(clk), .Q({display_digit, counter_1_q}), .carry(mode), .clk(clk), .clr(or_1_out));  // open: load, D
  or or_1 (or_1_out, clr, display_pattern);
  not not_1 (not_1_out, digit_solved);
  or or_2 (or_2_out, clr, digit_wrong, pattern_solved);
  _2_bit_equal u_2_bit_equal_1 (.A(expected), .B(selected_btn), .isEqual(n2_bit_equal_1_isequal));
  _2_bit_equal u_2_bit_equal_2 (.A(current_digit), .B(2'b11), .isEqual(n2_bit_equal_2_isequal));
  Register #(.width(32)) register_1 (.D(data), .en(wr_en), .Q(register_1_q), .clk(clk), .clr(clr));
  custom_counter custom_counter_1 (.clk(not_1_out), .in(1'b1), .en(1'b1), .clr(or_2_out), .count(current_digit));
  // Probe on current_digit
  and and_1 (digit_solved, n2_bit_equal_1_isequal, selection_made);
  not not_2 (not_2_out, n2_bit_equal_1_isequal);
  and and_2 (digit_wrong, selection_made, not_2_out);
  and and_3 (pattern_solved, n2_bit_equal_2_isequal, digit_solved);
  Multiplexer #(.select(2), .width(8)) multiplexer_1 (
    .in0(register_1_q[7:0]), .in1(register_1_q[15:8]), .in2(register_1_q[23:16]), .in3(register_1_q[31:24]),
    .out(multiplexer_1_out), .sel(current_pattern));  // open: en
  D_Flip_Flop #(.trigger("high")) d_ff_1 (
    .clk(module_solved), .D(module_solved), .Q(solved), .en(module_solved), .reset(clr));  // open: Qn, preset
  light_control light_control_1 (
    .light_sel(display_value), .b0(B0), .b1(B1), .b2(B2), .b3(B3), .L0(L0), .L1(L1), .L2(L2), .L3(L3),
    .mode(mode), .btn_pressed(btn_pressed), .btn(selected_btn));
  and and_4 (selection_made, btn_pressed, mode);
  Counter #(.width(3), .max('h4), .ongoal("stay"), .trigger("falling")) u_current_pattern (
    .count(1'b1), .Q({current_pattern_q[2], current_pattern}), .carry(module_solved), .clk(pattern_solved),
    .clr(clr));  // open: load, D
  Multiplexer #(.select(2), .width(2)) multiplexer_2 (
    .in0(multiplexer_1_out[1:0]), .in1(multiplexer_1_out[3:2]), .in2(multiplexer_1_out[5:4]),
    .in3(multiplexer_1_out[7:6]), .out(display_value), .sel(display_digit));  // open: en
  Multiplexer #(.select(2), .width(2)) multiplexer_3 (
    .in0(multiplexer_1_out[1:0]), .in1(multiplexer_1_out[3:2]), .in2(multiplexer_1_out[5:4]),
    .in3(multiplexer_1_out[7:6]), .out(expected), .sel(current_digit));  // open: en

  // Other names for the same wires on the sheet: pattern_data[31:0] = data; reset = clr; write = wr_en

  // Notes on the sheet:
  //    on the LEDs below.
  //   Repeat until you have solved all four patterns.
  //   HOW TO PLAY
  //   Upon pressing the "display pattern" button, a 4-light pattern will be shown
  //   Light up the LEDs in the same order by pressing the corresponding buttons.
  //   SOLVE THIS
  //   Click button to see current pattern
endmodule

module RegisterFile (
  input  [31:0] WriteData,
  input  RegWriteEnable,
  input  [4:0] WriteReg,
  input  clk,
  input  reset,
  input  [4:0] ReadReg2,
  input  [4:0] ReadReg1,
  output [31:0] ReadData2,
  output [31:0] ReadData1
);

  wire and_1_out, decoder_1_out1, decoder_1_out2, decoder_1_out3, decoder_1_out4, decoder_1_out5,
       decoder_1_out6, decoder_1_out7, decoder_1_out8, decoder_1_out9, decoder_1_out10, decoder_1_out11,
       decoder_1_out12, decoder_1_out13, decoder_1_out14, decoder_1_out15, decoder_1_out16, decoder_1_out17,
       decoder_1_out18, decoder_1_out19, decoder_1_out20, decoder_1_out21, decoder_1_out22, decoder_1_out23,
       decoder_1_out24, decoder_1_out25, decoder_1_out26, decoder_1_out27, decoder_1_out28, decoder_1_out29,
       decoder_1_out30, decoder_1_out31, decoder_2_out0, decoder_2_out1, decoder_2_out2, decoder_2_out3,
       decoder_2_out4, decoder_2_out5, decoder_2_out6, decoder_2_out7, decoder_2_out8, decoder_2_out9,
       decoder_2_out10, decoder_2_out11, decoder_2_out12, decoder_2_out13, decoder_2_out14, decoder_2_out15,
       decoder_2_out16, decoder_2_out17, decoder_2_out18, decoder_2_out19, decoder_2_out20, decoder_2_out21,
       decoder_2_out22, decoder_2_out23, decoder_2_out24, decoder_2_out25, decoder_2_out26, decoder_2_out27,
       decoder_2_out28, decoder_2_out29, decoder_2_out30, decoder_2_out31, decoder_3_out0, decoder_3_out1,
       decoder_3_out2, decoder_3_out3, decoder_3_out4, decoder_3_out5, decoder_3_out6, decoder_3_out7,
       decoder_3_out8, decoder_3_out9, decoder_3_out10, decoder_3_out11, decoder_3_out12, decoder_3_out13,
       decoder_3_out14, decoder_3_out15, decoder_3_out16, decoder_3_out17, decoder_3_out18, decoder_3_out19,
       decoder_3_out20, decoder_3_out21, decoder_3_out22, decoder_3_out23, decoder_3_out24, decoder_3_out25,
       decoder_3_out26, decoder_3_out27, decoder_3_out28, decoder_3_out29, decoder_3_out30, decoder_3_out31,
       enab, not_1_out;
  wire [31:0] _0, _1, _2, _3, _4, _5, _6, _7, _8, _9, _10, _11, _12, _13, _14, _15, _16, _17, _18, _19, _20,
       _21, _22, _23, _24, _25, _26, _27, _28, _29, _30, _31;

  assign ReadData2 = decoder_2_out0 ? _0 : 32'bz;  // Controlled_Buffer controlled_buffer_1
  assign ReadData1 = decoder_3_out0 ? _0 : 32'bz;  // Controlled_Buffer controlled_buffer_2
  Decoder #(.select(5), .enable("false")) decoder_1 (
    .out1(decoder_1_out1), .out2(decoder_1_out2), .out3(decoder_1_out3), .out4(decoder_1_out4),
    .out5(decoder_1_out5), .out6(decoder_1_out6), .out7(decoder_1_out7), .out8(decoder_1_out8),
    .out9(decoder_1_out9), .out10(decoder_1_out10), .out11(decoder_1_out11), .out12(decoder_1_out12),
    .out13(decoder_1_out13), .out14(decoder_1_out14), .out15(decoder_1_out15), .out16(decoder_1_out16),
    .out17(decoder_1_out17), .out18(decoder_1_out18), .out19(decoder_1_out19), .out20(decoder_1_out20),
    .out21(decoder_1_out21), .out22(decoder_1_out22), .out23(decoder_1_out23), .out24(decoder_1_out24),
    .out25(decoder_1_out25), .out26(decoder_1_out26), .out27(decoder_1_out27), .out28(decoder_1_out28),
    .out29(decoder_1_out29), .out30(decoder_1_out30), .out31(decoder_1_out31), .sel(WriteReg));  // open: out0
  assign ReadData2 = decoder_2_out1 ? _1 : 32'bz;  // Controlled_Buffer controlled_buffer_3
  assign ReadData1 = decoder_3_out1 ? _1 : 32'bz;  // Controlled_Buffer controlled_buffer_4
  register_32 register_32_1 (.clk(and_1_out), .\input (WriteData), .enable(1'b0), .\output (_0), .reset(reset));
  register_32 register_32_2 (
    .clk(and_1_out), .\input (WriteData), .enable(decoder_1_out1), .\output (_1), .reset(reset));
  register_32 register_32_3 (
    .clk(and_1_out), .\input (WriteData), .enable(decoder_1_out2), .\output (_2), .reset(reset));
  register_32 register_32_4 (
    .clk(and_1_out), .\input (WriteData), .enable(decoder_1_out3), .\output (_3), .reset(reset));
  register_32 register_32_5 (
    .clk(and_1_out), .\input (WriteData), .enable(decoder_1_out4), .\output (_4), .reset(reset));
  register_32 register_32_6 (
    .clk(and_1_out), .\input (WriteData), .enable(decoder_1_out5), .\output (_5), .reset(reset));
  register_32 register_32_7 (
    .clk(and_1_out), .\input (WriteData), .enable(decoder_1_out6), .\output (_6), .reset(reset));
  register_32 register_32_8 (
    .clk(and_1_out), .\input (WriteData), .enable(decoder_1_out7), .\output (_7), .reset(reset));
  and and_1 (and_1_out, clk, enab);
  assign ReadData2 = decoder_2_out3 ? _3 : 32'bz;  // Controlled_Buffer controlled_buffer_5
  assign ReadData2 = decoder_2_out2 ? _2 : 32'bz;  // Controlled_Buffer controlled_buffer_6
  assign ReadData1 = decoder_3_out3 ? _3 : 32'bz;  // Controlled_Buffer controlled_buffer_7
  assign ReadData1 = decoder_3_out2 ? _2 : 32'bz;  // Controlled_Buffer controlled_buffer_8
  assign ReadData2 = decoder_2_out4 ? _4 : 32'bz;  // Controlled_Buffer controlled_buffer_9
  assign ReadData1 = decoder_3_out5 ? _5 : 32'bz;  // Controlled_Buffer controlled_buffer_10
  assign ReadData1 = decoder_3_out4 ? _4 : 32'bz;  // Controlled_Buffer controlled_buffer_11
  assign ReadData2 = decoder_2_out6 ? _6 : 32'bz;  // Controlled_Buffer controlled_buffer_12
  assign ReadData2 = decoder_2_out5 ? _5 : 32'bz;  // Controlled_Buffer controlled_buffer_13
  assign ReadData1 = decoder_3_out6 ? _6 : 32'bz;  // Controlled_Buffer controlled_buffer_14
  register_32 register_32_9 (
    .clk(and_1_out), .\input (WriteData), .enable(decoder_1_out8), .\output (_8), .reset(reset));
  register_32 register_32_10 (
    .clk(and_1_out), .\input (WriteData), .enable(decoder_1_out9), .\output (_9), .reset(reset));
  register_32 register_32_11 (
    .clk(and_1_out), .\input (WriteData), .enable(decoder_1_out10), .\output (_10), .reset(reset));
  register_32 register_32_12 (
    .clk(and_1_out), .\input (WriteData), .enable(decoder_1_out11), .\output (_11), .reset(reset));
  register_32 register_32_13 (
    .clk(and_1_out), .\input (WriteData), .enable(decoder_1_out12), .\output (_12), .reset(reset));
  register_32 register_32_14 (
    .clk(and_1_out), .\input (WriteData), .enable(decoder_1_out13), .\output (_13), .reset(reset));
  register_32 register_32_15 (
    .clk(and_1_out), .\input (WriteData), .enable(decoder_1_out14), .\output (_14), .reset(reset));
  register_32 register_32_16 (
    .clk(and_1_out), .\input (WriteData), .enable(decoder_1_out15), .\output (_15), .reset(reset));
  assign ReadData2 = decoder_2_out7 ? _7 : 32'bz;  // Controlled_Buffer controlled_buffer_15
  assign ReadData2 = decoder_2_out8 ? _8 : 32'bz;  // Controlled_Buffer controlled_buffer_16
  assign ReadData1 = decoder_3_out8 ? _8 : 32'bz;  // Controlled_Buffer controlled_buffer_17
  assign ReadData1 = decoder_3_out7 ? _7 : 32'bz;  // Controlled_Buffer controlled_buffer_18
  assign ReadData2 = decoder_2_out9 ? _9 : 32'bz;  // Controlled_Buffer controlled_buffer_19
  assign ReadData1 = decoder_3_out9 ? _9 : 32'bz;  // Controlled_Buffer controlled_buffer_20
  assign ReadData2 = decoder_2_out11 ? _11 : 32'bz;  // Controlled_Buffer controlled_buffer_21
  assign ReadData2 = decoder_2_out10 ? _10 : 32'bz;  // Controlled_Buffer controlled_buffer_22
  assign ReadData1 = decoder_3_out11 ? _11 : 32'bz;  // Controlled_Buffer controlled_buffer_23
  assign ReadData1 = decoder_3_out10 ? _10 : 32'bz;  // Controlled_Buffer controlled_buffer_24
  assign ReadData2 = decoder_2_out12 ? _12 : 32'bz;  // Controlled_Buffer controlled_buffer_25
  assign ReadData1 = decoder_3_out12 ? _12 : 32'bz;  // Controlled_Buffer controlled_buffer_26
  assign ReadData1 = decoder_3_out13 ? _13 : 32'bz;  // Controlled_Buffer controlled_buffer_27
  register_32 register_32_17 (
    .clk(and_1_out), .\input (WriteData), .enable(decoder_1_out16), .\output (_16), .reset(reset));
  register_32 register_32_18 (
    .clk(and_1_out), .\input (WriteData), .enable(decoder_1_out17), .\output (_17), .reset(reset));
  register_32 register_32_19 (
    .clk(and_1_out), .\input (WriteData), .enable(decoder_1_out18), .\output (_18), .reset(reset));
  register_32 register_32_20 (
    .clk(and_1_out), .\input (WriteData), .enable(decoder_1_out19), .\output (_19), .reset(reset));
  register_32 register_32_21 (
    .clk(and_1_out), .\input (WriteData), .enable(decoder_1_out20), .\output (_20), .reset(reset));
  register_32 register_32_22 (
    .clk(and_1_out), .\input (WriteData), .enable(decoder_1_out21), .\output (_21), .reset(reset));
  register_32 register_32_23 (
    .clk(and_1_out), .\input (WriteData), .enable(decoder_1_out22), .\output (_22), .reset(reset));
  register_32 register_32_24 (
    .clk(and_1_out), .\input (WriteData), .enable(decoder_1_out23), .\output (_23), .reset(reset));
  assign ReadData2 = decoder_2_out14 ? _14 : 32'bz;  // Controlled_Buffer controlled_buffer_28
  assign ReadData2 = decoder_2_out13 ? _13 : 32'bz;  // Controlled_Buffer controlled_buffer_29
  Decoder #(.select(5), .enable("false")) decoder_2 (
    .out0(decoder_2_out0), .out1(decoder_2_out1), .out2(decoder_2_out2), .out3(decoder_2_out3),
    .out4(decoder_2_out4), .out5(decoder_2_out5), .out6(decoder_2_out6), .out7(decoder_2_out7),
    .out8(decoder_2_out8), .out9(decoder_2_out9), .out10(decoder_2_out10), .out11(decoder_2_out11),
    .out12(decoder_2_out12), .out13(decoder_2_out13), .out14(decoder_2_out14), .out15(decoder_2_out15),
    .out16(decoder_2_out16), .out17(decoder_2_out17), .out18(decoder_2_out18), .out19(decoder_2_out19),
    .out20(decoder_2_out20), .out21(decoder_2_out21), .out22(decoder_2_out22), .out23(decoder_2_out23),
    .out24(decoder_2_out24), .out25(decoder_2_out25), .out26(decoder_2_out26), .out27(decoder_2_out27),
    .out28(decoder_2_out28), .out29(decoder_2_out29), .out30(decoder_2_out30), .out31(decoder_2_out31),
    .sel(ReadReg2));
  assign ReadData1 = decoder_3_out14 ? _14 : 32'bz;  // Controlled_Buffer controlled_buffer_30
  Decoder #(.select(5), .enable("false")) decoder_3 (
    .out0(decoder_3_out0), .out1(decoder_3_out1), .out2(decoder_3_out2), .out3(decoder_3_out3),
    .out4(decoder_3_out4), .out5(decoder_3_out5), .out6(decoder_3_out6), .out7(decoder_3_out7),
    .out8(decoder_3_out8), .out9(decoder_3_out9), .out10(decoder_3_out10), .out11(decoder_3_out11),
    .out12(decoder_3_out12), .out13(decoder_3_out13), .out14(decoder_3_out14), .out15(decoder_3_out15),
    .out16(decoder_3_out16), .out17(decoder_3_out17), .out18(decoder_3_out18), .out19(decoder_3_out19),
    .out20(decoder_3_out20), .out21(decoder_3_out21), .out22(decoder_3_out22), .out23(decoder_3_out23),
    .out24(decoder_3_out24), .out25(decoder_3_out25), .out26(decoder_3_out26), .out27(decoder_3_out27),
    .out28(decoder_3_out28), .out29(decoder_3_out29), .out30(decoder_3_out30), .out31(decoder_3_out31),
    .sel(ReadReg1));
  assign ReadData2 = decoder_2_out15 ? _15 : 32'bz;  // Controlled_Buffer controlled_buffer_31
  assign ReadData1 = decoder_3_out15 ? _15 : 32'bz;  // Controlled_Buffer controlled_buffer_32
  assign ReadData2 = decoder_2_out16 ? _16 : 32'bz;  // Controlled_Buffer controlled_buffer_33
  assign ReadData1 = decoder_3_out16 ? _16 : 32'bz;  // Controlled_Buffer controlled_buffer_34
  register_32 register_32_25 (
    .clk(and_1_out), .\input (WriteData), .enable(decoder_1_out24), .\output (_24), .reset(reset));
  register_32 register_32_26 (
    .clk(and_1_out), .\input (WriteData), .enable(decoder_1_out25), .\output (_25), .reset(reset));
  register_32 register_32_27 (
    .clk(and_1_out), .\input (WriteData), .enable(decoder_1_out26), .\output (_26), .reset(reset));
  register_32 register_32_28 (
    .clk(and_1_out), .\input (WriteData), .enable(decoder_1_out27), .\output (_27), .reset(reset));
  register_32 register_32_29 (
    .clk(and_1_out), .\input (WriteData), .enable(decoder_1_out28), .\output (_28), .reset(reset));
  register_32 register_32_30 (
    .clk(and_1_out), .\input (WriteData), .enable(decoder_1_out29), .\output (_29), .reset(reset));
  register_32 register_32_31 (
    .clk(and_1_out), .\input (WriteData), .enable(decoder_1_out30), .\output (_30), .reset(reset));
  register_32 register_32_32 (
    .clk(and_1_out), .\input (WriteData), .enable(decoder_1_out31), .\output (_31), .reset(reset));
  assign ReadData2 = decoder_2_out18 ? _18 : 32'bz;  // Controlled_Buffer controlled_buffer_35
  assign ReadData2 = decoder_2_out17 ? _17 : 32'bz;  // Controlled_Buffer controlled_buffer_36
  assign ReadData1 = decoder_3_out18 ? _18 : 32'bz;  // Controlled_Buffer controlled_buffer_37
  assign ReadData1 = decoder_3_out17 ? _17 : 32'bz;  // Controlled_Buffer controlled_buffer_38
  assign ReadData2 = decoder_2_out19 ? _19 : 32'bz;  // Controlled_Buffer controlled_buffer_39
  assign ReadData1 = decoder_3_out19 ? _19 : 32'bz;  // Controlled_Buffer controlled_buffer_40
  assign ReadData1 = decoder_3_out20 ? _20 : 32'bz;  // Controlled_Buffer controlled_buffer_41
  assign ReadData2 = decoder_2_out21 ? _21 : 32'bz;  // Controlled_Buffer controlled_buffer_42
  assign ReadData2 = decoder_2_out20 ? _20 : 32'bz;  // Controlled_Buffer controlled_buffer_43
  assign ReadData1 = decoder_3_out21 ? _21 : 32'bz;  // Controlled_Buffer controlled_buffer_44
  not not_1 (not_1_out, clk);
  assign ReadData2 = decoder_2_out22 ? _22 : 32'bz;  // Controlled_Buffer controlled_buffer_45
  assign ReadData2 = decoder_2_out23 ? _23 : 32'bz;  // Controlled_Buffer controlled_buffer_46
  assign ReadData1 = decoder_3_out22 ? _22 : 32'bz;  // Controlled_Buffer controlled_buffer_47
  assign ReadData1 = decoder_3_out23 ? _23 : 32'bz;  // Controlled_Buffer controlled_buffer_48
  and and_2 (enab, RegWriteEnable, not_1_out);
  assign ReadData2 = decoder_2_out24 ? _24 : 32'bz;  // Controlled_Buffer controlled_buffer_49
  assign ReadData1 = decoder_3_out24 ? _24 : 32'bz;  // Controlled_Buffer controlled_buffer_50
  // Probe on _0
  // Probe on _1
  // Probe on _2
  // Probe on _3
  // Probe on _4
  // Probe on _5
  // Probe on _6
  // Probe on _7
  assign ReadData2 = decoder_2_out26 ? _26 : 32'bz;  // Controlled_Buffer controlled_buffer_51
  assign ReadData2 = decoder_2_out25 ? _25 : 32'bz;  // Controlled_Buffer controlled_buffer_52
  assign ReadData1 = decoder_3_out25 ? _25 : 32'bz;  // Controlled_Buffer controlled_buffer_53
  assign ReadData1 = decoder_3_out26 ? _26 : 32'bz;  // Controlled_Buffer controlled_buffer_54
  assign ReadData2 = decoder_2_out27 ? _27 : 32'bz;  // Controlled_Buffer controlled_buffer_55
  assign ReadData1 = decoder_3_out27 ? _27 : 32'bz;  // Controlled_Buffer controlled_buffer_56
  assign ReadData1 = decoder_3_out28 ? _28 : 32'bz;  // Controlled_Buffer controlled_buffer_57
  assign ReadData2 = decoder_2_out29 ? _29 : 32'bz;  // Controlled_Buffer controlled_buffer_58
  assign ReadData2 = decoder_2_out28 ? _28 : 32'bz;  // Controlled_Buffer controlled_buffer_59
  assign ReadData1 = decoder_3_out29 ? _29 : 32'bz;  // Controlled_Buffer controlled_buffer_60
  // Probe on _8
  // Probe on _9
  // Probe on _10
  // Probe on _11
  // Probe on _12
  // Probe on _13
  // Probe on _14
  // Probe on _15
  assign ReadData2 = decoder_2_out31 ? _31 : 32'bz;  // Controlled_Buffer controlled_buffer_61
  assign ReadData2 = decoder_2_out30 ? _30 : 32'bz;  // Controlled_Buffer controlled_buffer_62
  assign ReadData1 = decoder_3_out31 ? _31 : 32'bz;  // Controlled_Buffer controlled_buffer_63
  assign ReadData1 = decoder_3_out30 ? _30 : 32'bz;  // Controlled_Buffer controlled_buffer_64
  // Probe on _16
  // Probe on _17
  // Probe on _18
  // Probe on _19
  // Probe on _20
  // Probe on _21
  // Probe on _22
  // Probe on _23
  // Probe on _24
  // Probe on _25
  // Probe on _26
  // Probe on _27
  // Probe on _28
  // Probe on _29
  // Probe on _30
  // Probe on _31

  // Other names for the same wires on the sheet: data[31:0] = WriteData
endmodule

module register_32 (
  input  enable,
  input  reset,
  input  clk,
  input  [31:0] \input ,
  output [31:0] \output 
);

  wire enable_t, not_1_out;

  not not_1 (not_1_out, clk);
  and and_1 (enable_t, not_1_out, enable);
  D_Flip_Flop d_ff_1 (.clk(clk), .D(\input [0]), .Q(\output [0]), .en(enable_t), .reset(reset));  // open: Qn, preset
  D_Flip_Flop d_ff_2 (.clk(clk), .D(\input [1]), .Q(\output [1]), .en(enable_t), .reset(reset));  // open: Qn, preset
  D_Flip_Flop d_ff_3 (.clk(clk), .D(\input [2]), .Q(\output [2]), .en(enable_t), .reset(reset));  // open: Qn, preset
  D_Flip_Flop d_ff_4 (.clk(clk), .D(\input [3]), .Q(\output [3]), .en(enable_t), .reset(reset));  // open: Qn, preset
  D_Flip_Flop d_ff_5 (.clk(clk), .D(\input [4]), .Q(\output [4]), .en(enable_t), .reset(reset));  // open: Qn, preset
  D_Flip_Flop d_ff_6 (.clk(clk), .D(\input [5]), .Q(\output [5]), .en(enable_t), .reset(reset));  // open: Qn, preset
  D_Flip_Flop d_ff_7 (.clk(clk), .D(\input [6]), .Q(\output [6]), .en(enable_t), .reset(reset));  // open: Qn, preset
  D_Flip_Flop d_ff_8 (.clk(clk), .D(\input [7]), .Q(\output [7]), .en(enable_t), .reset(reset));  // open: Qn, preset
  D_Flip_Flop d_ff_9 (.clk(clk), .D(\input [16]), .Q(\output [16]), .en(enable_t), .reset(reset));  // open: Qn, preset
  D_Flip_Flop d_ff_10 (.clk(clk), .D(\input [17]), .Q(\output [17]), .en(enable_t), .reset(reset));  // open: Qn, preset
  D_Flip_Flop d_ff_11 (.clk(clk), .D(\input [18]), .Q(\output [18]), .en(enable_t), .reset(reset));  // open: Qn, preset
  D_Flip_Flop d_ff_12 (.clk(clk), .D(\input [19]), .Q(\output [19]), .en(enable_t), .reset(reset));  // open: Qn, preset
  D_Flip_Flop d_ff_13 (.clk(clk), .D(\input [20]), .Q(\output [20]), .en(enable_t), .reset(reset));  // open: Qn, preset
  D_Flip_Flop d_ff_14 (.clk(clk), .D(\input [21]), .Q(\output [21]), .en(enable_t), .reset(reset));  // open: Qn, preset
  D_Flip_Flop d_ff_15 (.clk(clk), .D(\input [22]), .Q(\output [22]), .en(enable_t), .reset(reset));  // open: Qn, preset
  D_Flip_Flop d_ff_16 (.clk(clk), .D(\input [23]), .Q(\output [23]), .en(enable_t), .reset(reset));  // open: Qn, preset
  D_Flip_Flop d_ff_17 (.clk(clk), .D(\input [8]), .Q(\output [8]), .en(enable_t), .reset(reset));  // open: Qn, preset
  D_Flip_Flop d_ff_18 (.clk(clk), .D(\input [9]), .Q(\output [9]), .en(enable_t), .reset(reset));  // open: Qn, preset
  D_Flip_Flop d_ff_19 (.clk(clk), .D(\input [10]), .Q(\output [10]), .en(enable_t), .reset(reset));  // open: Qn, preset
  D_Flip_Flop d_ff_20 (.clk(clk), .D(\input [11]), .Q(\output [11]), .en(enable_t), .reset(reset));  // open: Qn, preset
  D_Flip_Flop d_ff_21 (.clk(clk), .D(\input [12]), .Q(\output [12]), .en(enable_t), .reset(reset));  // open: Qn, preset
  D_Flip_Flop d_ff_22 (.clk(clk), .D(\input [13]), .Q(\output [13]), .en(enable_t), .reset(reset));  // open: Qn, preset
  D_Flip_Flop d_ff_23 (.clk(clk), .D(\input [14]), .Q(\output [14]), .en(enable_t), .reset(reset));  // open: Qn, preset
  D_Flip_Flop d_ff_24 (.clk(clk), .D(\input [15]), .Q(\output [15]), .en(enable_t), .reset(reset));  // open: Qn, preset
  D_Flip_Flop d_ff_25 (.clk(clk), .D(\input [24]), .Q(\output [24]), .en(enable_t), .reset(reset));  // open: Qn, preset
  D_Flip_Flop d_ff_26 (.clk(clk), .D(\input [25]), .Q(\output [25]), .en(enable_t), .reset(reset));  // open: Qn, preset
  D_Flip_Flop d_ff_27 (.clk(clk), .D(\input [26]), .Q(\output [26]), .en(enable_t), .reset(reset));  // open: Qn, preset
  D_Flip_Flop d_ff_28 (.clk(clk), .D(\input [27]), .Q(\output [27]), .en(enable_t), .reset(reset));  // open: Qn, preset
  D_Flip_Flop d_ff_29 (.clk(clk), .D(\input [28]), .Q(\output [28]), .en(enable_t), .reset(reset));  // open: Qn, preset
  D_Flip_Flop d_ff_30 (.clk(clk), .D(\input [29]), .Q(\output [29]), .en(enable_t), .reset(reset));  // open: Qn, preset
  D_Flip_Flop d_ff_31 (.clk(clk), .D(\input [30]), .Q(\output [30]), .en(enable_t), .reset(reset));  // open: Qn, preset
  D_Flip_Flop d_ff_32 (.clk(clk), .D(\input [31]), .Q(\output [31]), .en(enable_t), .reset(reset));  // open: Qn, preset

  // Other names for the same wires on the sheet: first[7:0] = \input [7:0]; second[7:0] = \input [15:8];
  //   third[7:0] = \input [23:16]; fourth[7:0] = \input [31:24]
endmodule

module ALU (
  input  [4:0] shift,
  input  [31:0] InputData1,
  input  [31:0] InputData2,
  input  [4:0] ALUop,
  output ovf,
  output BNE,
  output BLT,
  output [31:0] out_8
);

  wire comparator_1_eq, n32_bit_compact_1_ovf, n32_bit_compact_2_ovf;
  wire [31:0] and_1_out, n32_bit_compact_1_result, n32_bit_compact_2_result, or_1_out, shifter_1_out,
       shifter_2_out;

  Shifter #(.width(32)) shifter_1 (.in(InputData1), .\dist (shift), .out(shifter_1_out));
  Shifter #(.width(32), .shift("ar")) shifter_2 (.in(InputData1), .\dist (shift), .out(shifter_2_out));
  _32_bit_compact u_32_bit_compact_1 (
    .result(n32_bit_compact_1_result), .A(InputData1), .B(InputData2), .ovf(n32_bit_compact_1_ovf), .sub(1'b0));
  _32_bit_compact u_32_bit_compact_2 (
    .result(n32_bit_compact_2_result), .A(InputData1), .B(InputData2), .ovf(n32_bit_compact_2_ovf), .sub(1'b1));
  assign and_1_out = InputData1 & InputData2;  // AND_Gate and_1, 32 bits wide
  assign or_1_out = InputData1 | InputData2;  // OR_Gate or_1, 32 bits wide
  or or_2 (ovf, n32_bit_compact_2_ovf, n32_bit_compact_1_ovf);
  Multiplexer #(.select(5), .width(32), .enable("false")) multiplexer_1 (
    .in0(n32_bit_compact_1_result), .in1(n32_bit_compact_2_result), .in2(and_1_out), .in3(or_1_out),
    .in4(shifter_1_out), .in5(shifter_2_out), .out(out_8), .sel(ALUop));  // open: in6, in7, in8, in9, in10, in11, in12, in13, in14, in15, in16, in17, in18, in19, in20, in21, in22, in23, in24, in25, in26, in27, in28, in29, in30, in31
  Comparator #(.width(32)) comparator_1 (.a(InputData1), .b(InputData2), .eq(comparator_1_eq), .lt(BLT));  // open: gt
  not not_1 (BNE, comparator_1_eq);

  // Other names for the same wires on the sheet: A[31:0] = InputData1; B[31:0] = InputData2
endmodule

module one_bit_add (
  input  cin,
  input  a,
  input  b,
  output cout,
  output sum
);

  wire and_1_out, and_2_out, xor_1_out;

  or or_1 (cout, and_1_out, and_2_out);
  xor xor_1 (xor_1_out, a, b);
  and and_1 (and_1_out, a, b);
  and and_2 (and_2_out, xor_1_out, cin);
  xor xor_2 (sum, cin, xor_1_out);
endmodule

module _32_bit_add (
  input  a31,
  input  b31,
  input  a30,
  input  b30,
  input  a29,
  input  b29,
  input  a28,
  input  b28,
  input  a27,
  input  b27,
  input  a26,
  input  b26,
  input  a25,
  input  b25,
  input  a24,
  input  b24,
  input  a23,
  input  b23,
  input  a22,
  input  b22,
  input  a21,
  input  b21,
  input  a20,
  input  b20,
  input  a19,
  input  b19,
  input  a18,
  input  b18,
  input  a17,
  input  b17,
  input  a16,
  input  b16,
  input  add_sub,
  input  a15,
  input  b15,
  input  a14,
  input  b14,
  input  a13,
  input  b13,
  input  a12,
  input  b12,
  input  a11,
  input  b11,
  input  a10,
  input  b10,
  input  a9,
  input  b9,
  input  a8,
  input  b8,
  input  a7,
  input  b7,
  input  a6,
  input  b6,
  input  a5,
  input  b5,
  input  a4,
  input  b4,
  input  a3,
  input  b3,
  input  a2,
  input  b2,
  input  a1,
  input  b1,
  input  a0,
  input  b0,
  output ovf,
  output s31,
  output s30,
  output s29,
  output s28,
  output s27,
  output s26,
  output s25,
  output s24,
  output cout,
  output s23,
  output s22,
  output s21,
  output s20,
  output s19,
  output s18,
  output s17,
  output s16,
  output s15,
  output s14,
  output s13,
  output s12,
  output s11,
  output s10,
  output s9,
  output s8,
  output s7,
  output s6,
  output s5,
  output s4,
  output s3,
  output s2,
  output s1,
  output s0
);

  wire one_bit_add_2_cout, one_bit_add_3_cout, one_bit_add_4_cout, one_bit_add_5_cout, one_bit_add_6_cout,
       one_bit_add_7_cout, one_bit_add_8_cout, one_bit_add_9_cout, one_bit_add_10_cout, one_bit_add_11_cout,
       one_bit_add_12_cout, one_bit_add_13_cout, one_bit_add_14_cout, one_bit_add_15_cout,
       one_bit_add_16_cout, one_bit_add_17_cout, one_bit_add_18_cout, one_bit_add_19_cout,
       one_bit_add_20_cout, one_bit_add_21_cout, one_bit_add_22_cout, one_bit_add_23_cout,
       one_bit_add_24_cout, one_bit_add_25_cout, one_bit_add_26_cout, one_bit_add_27_cout,
       one_bit_add_28_cout, one_bit_add_29_cout, one_bit_add_30_cout, one_bit_add_31_cout,
       one_bit_add_32_cout, xor_2_out, xor_3_out, xor_4_out, xor_5_out, xor_6_out, xor_7_out, xor_8_out,
       xor_9_out, xor_10_out, xor_11_out, xor_12_out, xor_13_out, xor_14_out, xor_15_out, xor_16_out,
       xor_17_out, xor_18_out, xor_19_out, xor_20_out, xor_21_out, xor_22_out, xor_23_out, xor_24_out,
       xor_25_out, xor_26_out, xor_27_out, xor_28_out, xor_29_out, xor_30_out, xor_31_out, xor_32_out,
       xor_33_out;

  xor xor_1 (ovf, cout, one_bit_add_5_cout);
  one_bit_add one_bit_add_1 (.a(a31), .b(xor_2_out), .cout(cout), .cin(one_bit_add_5_cout), .sum(s31));
  xor xor_2 (xor_2_out, add_sub, b31);
  one_bit_add one_bit_add_2 (.a(a23), .b(xor_3_out), .cout(one_bit_add_2_cout), .cin(one_bit_add_6_cout), .sum(s23));
  xor xor_3 (xor_3_out, add_sub, b23);
  one_bit_add one_bit_add_3 (.a(a15), .b(xor_4_out), .cout(one_bit_add_3_cout), .cin(one_bit_add_7_cout), .sum(s15));
  xor xor_4 (xor_4_out, add_sub, b15);
  one_bit_add one_bit_add_4 (.a(a7), .b(xor_5_out), .cout(one_bit_add_4_cout), .cin(one_bit_add_8_cout), .sum(s7));
  xor xor_5 (xor_5_out, add_sub, b7);
  one_bit_add one_bit_add_5 (.a(a30), .b(xor_6_out), .cout(one_bit_add_5_cout), .cin(one_bit_add_9_cout), .sum(s30));
  xor xor_6 (xor_6_out, add_sub, b30);
  one_bit_add one_bit_add_6 (.a(a22), .b(xor_7_out), .cout(one_bit_add_6_cout), .cin(one_bit_add_10_cout), .sum(s22));
  xor xor_7 (xor_7_out, add_sub, b22);
  one_bit_add one_bit_add_7 (.a(a14), .b(xor_8_out), .cout(one_bit_add_7_cout), .cin(one_bit_add_11_cout), .sum(s14));
  xor xor_8 (xor_8_out, add_sub, b14);
  one_bit_add one_bit_add_8 (.a(a6), .b(xor_9_out), .cout(one_bit_add_8_cout), .cin(one_bit_add_12_cout), .sum(s6));
  xor xor_9 (xor_9_out, add_sub, b6);
  one_bit_add one_bit_add_9 (.a(a29), .b(xor_10_out), .cout(one_bit_add_9_cout), .cin(one_bit_add_13_cout), .sum(s29));
  xor xor_10 (xor_10_out, add_sub, b29);
  one_bit_add one_bit_add_10 (
    .a(a21), .b(xor_11_out), .cout(one_bit_add_10_cout), .cin(one_bit_add_14_cout), .sum(s21));
  xor xor_11 (xor_11_out, add_sub, b21);
  one_bit_add one_bit_add_11 (
    .a(a13), .b(xor_12_out), .cout(one_bit_add_11_cout), .cin(one_bit_add_15_cout), .sum(s13));
  xor xor_12 (xor_12_out, add_sub, b13);
  one_bit_add one_bit_add_12 (.a(a5), .b(xor_13_out), .cout(one_bit_add_12_cout), .cin(one_bit_add_16_cout), .sum(s5));
  xor xor_13 (xor_13_out, add_sub, b5);
  one_bit_add one_bit_add_13 (
    .a(a28), .b(xor_14_out), .cout(one_bit_add_13_cout), .cin(one_bit_add_17_cout), .sum(s28));
  xor xor_14 (xor_14_out, add_sub, b28);
  one_bit_add one_bit_add_14 (
    .a(a20), .b(xor_15_out), .cout(one_bit_add_14_cout), .cin(one_bit_add_18_cout), .sum(s20));
  xor xor_15 (xor_15_out, add_sub, b20);
  one_bit_add one_bit_add_15 (
    .a(a12), .b(xor_16_out), .cout(one_bit_add_15_cout), .cin(one_bit_add_19_cout), .sum(s12));
  xor xor_16 (xor_16_out, add_sub, b12);
  one_bit_add one_bit_add_16 (.a(a4), .b(xor_17_out), .cout(one_bit_add_16_cout), .cin(one_bit_add_20_cout), .sum(s4));
  one_bit_add one_bit_add_17 (
    .a(a27), .b(xor_18_out), .cout(one_bit_add_17_cout), .cin(one_bit_add_21_cout), .sum(s27));
  one_bit_add one_bit_add_18 (
    .a(a19), .b(xor_19_out), .cout(one_bit_add_18_cout), .cin(one_bit_add_22_cout), .sum(s19));
  one_bit_add one_bit_add_19 (
    .a(a11), .b(xor_20_out), .cout(one_bit_add_19_cout), .cin(one_bit_add_23_cout), .sum(s11));
  one_bit_add one_bit_add_20 (.a(a3), .b(xor_21_out), .cout(one_bit_add_20_cout), .cin(one_bit_add_25_cout), .sum(s3));
  xor xor_17 (xor_17_out, add_sub, b4);
  one_bit_add one_bit_add_21 (
    .a(a26), .b(xor_22_out), .cout(one_bit_add_21_cout), .cin(one_bit_add_24_cout), .sum(s26));
  xor xor_18 (xor_18_out, add_sub, b27);
  one_bit_add one_bit_add_22 (
    .a(a18), .b(xor_23_out), .cout(one_bit_add_22_cout), .cin(one_bit_add_26_cout), .sum(s18));
  xor xor_19 (xor_19_out, add_sub, b19);
  one_bit_add one_bit_add_23 (
    .a(a10), .b(xor_24_out), .cout(one_bit_add_23_cout), .cin(one_bit_add_27_cout), .sum(s10));
  xor xor_20 (xor_20_out, add_sub, b11);
  xor xor_21 (xor_21_out, add_sub, b3);
  one_bit_add one_bit_add_24 (
    .a(a25), .b(xor_26_out), .cout(one_bit_add_24_cout), .cin(one_bit_add_29_cout), .sum(s25));
  xor xor_22 (xor_22_out, add_sub, b26);
  xor xor_23 (xor_23_out, add_sub, b18);
  xor xor_24 (xor_24_out, add_sub, b10);
  one_bit_add one_bit_add_25 (.a(a2), .b(xor_25_out), .cout(one_bit_add_25_cout), .cin(one_bit_add_28_cout), .sum(s2));
  xor xor_25 (xor_25_out, add_sub, b2);
  xor xor_26 (xor_26_out, add_sub, b25);
  one_bit_add one_bit_add_26 (
    .a(a17), .b(xor_27_out), .cout(one_bit_add_26_cout), .cin(one_bit_add_30_cout), .sum(s17));
  xor xor_27 (xor_27_out, add_sub, b17);
  one_bit_add one_bit_add_27 (.a(a9), .b(xor_28_out), .cout(one_bit_add_27_cout), .cin(one_bit_add_31_cout), .sum(s9));
  xor xor_28 (xor_28_out, add_sub, b9);
  one_bit_add one_bit_add_28 (.a(a1), .b(xor_29_out), .cout(one_bit_add_28_cout), .cin(one_bit_add_32_cout), .sum(s1));
  xor xor_29 (xor_29_out, add_sub, b1);
  one_bit_add one_bit_add_29 (.a(a24), .b(xor_30_out), .cout(one_bit_add_29_cout), .cin(one_bit_add_2_cout), .sum(s24));
  xor xor_30 (xor_30_out, add_sub, b24);
  one_bit_add one_bit_add_30 (.a(a16), .b(xor_31_out), .cout(one_bit_add_30_cout), .cin(one_bit_add_3_cout), .sum(s16));
  xor xor_31 (xor_31_out, add_sub, b16);
  one_bit_add one_bit_add_31 (.a(a8), .b(xor_32_out), .cout(one_bit_add_31_cout), .cin(one_bit_add_4_cout), .sum(s8));
  xor xor_32 (xor_32_out, add_sub, b8);
  one_bit_add one_bit_add_32 (.a(a0), .b(xor_33_out), .cout(one_bit_add_32_cout), .cin(add_sub), .sum(s0));
  xor xor_33 (xor_33_out, add_sub, b0);
endmodule

module _32_bit_compact (
  input  [31:0] A,
  input  [31:0] B,
  input  sub,
  output ovf,
  output [31:0] result
);

  _32_bit_add u_32_bit_add_1 (
    .add_sub(sub), .ovf(ovf), .s7(result[7]), .s31(result[31]), .s23(result[23]), .s15(result[15]),
    .s30(result[30]), .s22(result[22]), .s14(result[14]), .s6(result[6]), .s29(result[29]), .s21(result[21]),
    .s13(result[13]), .s5(result[5]), .s28(result[28]), .s20(result[20]), .s12(result[12]), .s4(result[4]),
    .s27(result[27]), .s19(result[19]), .s11(result[11]), .s3(result[3]), .s26(result[26]), .s18(result[18]),
    .s10(result[10]), .s2(result[2]), .s25(result[25]), .s17(result[17]), .s9(result[9]), .s1(result[1]),
    .s24(result[24]), .s16(result[16]), .s8(result[8]), .s0(result[0]), .a31(A[31]), .a23(A[23]),
    .a15(A[15]), .a7(A[7]), .b31(B[31]), .b23(B[23]), .b15(B[15]), .b7(B[7]), .a30(A[30]), .a22(A[22]),
    .a14(A[14]), .a6(A[6]), .b30(B[30]), .b22(B[22]), .b14(B[14]), .b6(B[6]), .a29(A[29]), .a21(A[21]),
    .a13(A[13]), .a5(A[5]), .b29(B[29]), .b21(B[21]), .b13(B[13]), .b5(B[5]), .a28(A[28]), .a20(A[20]),
    .a12(A[12]), .a4(A[4]), .b28(B[28]), .b20(B[20]), .b12(B[12]), .b4(B[4]), .a27(A[27]), .a19(A[19]),
    .a11(A[11]), .a3(A[3]), .b27(B[27]), .b19(B[19]), .b11(B[11]), .b3(B[3]), .a26(A[26]), .a18(A[18]),
    .a10(A[10]), .a2(A[2]), .b26(B[26]), .b18(B[18]), .b10(B[10]), .b2(B[2]), .a25(A[25]), .a17(A[17]),
    .a9(A[9]), .a1(A[1]), .b25(B[25]), .b17(B[17]), .b9(B[9]), .b1(B[1]), .a24(A[24]), .a16(A[16]),
    .a8(A[8]), .a0(A[0]), .b24(B[24]), .b16(B[16]), .b8(B[8]), .b0(B[0]));  // open: cout
endmodule

module decoder (
  input  [4:0] opcode,
  output r,
  output addi,
  output sw,
  output lw,
  output j,
  output bne,
  output jal,
  output jr,
  output blt,
  output bex,
  output setx,
  output swtp,
  output swtc,
  output \rand 
);

  wire not_1_out, not_2_out, not_3_out, not_4_out, not_5_out;

  not not_1 (not_1_out, opcode[0]);
  not not_2 (not_2_out, opcode[1]);
  not not_3 (not_3_out, opcode[2]);
  not not_4 (not_4_out, opcode[3]);
  not not_5 (not_5_out, opcode[4]);
  and and_1 (r, not_1_out, not_2_out, not_3_out, not_4_out, not_5_out);
  and and_2 (addi, not_5_out, not_4_out, opcode[2], not_2_out, opcode[0]);
  and and_3 (sw, not_5_out, not_4_out, opcode[2], opcode[1], opcode[0]);
  and and_4 (lw, not_5_out, opcode[3], not_3_out, not_2_out, not_1_out);
  and and_5 (j, not_5_out, not_4_out, not_3_out, not_2_out, opcode[0]);
  and and_6 (bne, not_5_out, not_4_out, not_3_out, opcode[1], not_1_out);
  and and_7 (jal, not_5_out, not_4_out, not_3_out, opcode[1], opcode[0]);
  and and_8 (blt, not_5_out, not_4_out, opcode[2], opcode[1], not_1_out);
  and and_9 (jr, not_5_out, not_4_out, opcode[2], not_2_out, not_1_out);
  and and_10 (bex, opcode[4], not_4_out, opcode[2], opcode[1], not_1_out);
  and and_11 (setx, opcode[4], not_4_out, opcode[2], not_2_out, opcode[0]);
  and and_12 (swtp, opcode[4], opcode[3], not_3_out, not_2_out, not_1_out);
  and and_13 (swtc, opcode[4], opcode[3], not_3_out, opcode[1], not_1_out);
  and and_14 (\rand , opcode[4], opcode[3], not_3_out, opcode[1], opcode[0]);
endmodule

module r_decoder (
  input  [4:0] alu_opcode,
  output add,
  output sub,
  output \and ,
  output \or ,
  output sll,
  output sra
);

  wire not_1_out, not_2_out, not_3_out, not_4_out, not_5_out;

  not not_1 (not_1_out, alu_opcode[0]);
  not not_2 (not_2_out, alu_opcode[1]);
  not not_3 (not_3_out, alu_opcode[2]);
  not not_4 (not_4_out, alu_opcode[3]);
  not not_5 (not_5_out, alu_opcode[4]);
  and and_1 (add, not_5_out, not_4_out, not_3_out, not_2_out, not_1_out);
  and and_2 (sub, not_5_out, not_4_out, not_3_out, not_2_out, alu_opcode[0]);
  and and_3 (\and , not_5_out, not_4_out, not_3_out, alu_opcode[1], not_1_out);
  and and_4 (sll, not_5_out, not_4_out, alu_opcode[2], not_2_out, not_1_out);
  and and_5 (\or , not_5_out, not_4_out, not_3_out, alu_opcode[1], alu_opcode[0]);
  and and_6 (sra, not_5_out, not_4_out, alu_opcode[2], not_2_out, alu_opcode[0]);
endmodule

module _2_bit_equal (
  input  [1:0] A,
  input  [1:0] B,
  output isEqual
);

  wire xnor_1_out, xnor_2_out;

  xnor xnor_1 (xnor_1_out, A[0], B[0]);
  xnor xnor_2 (xnor_2_out, A[1], B[1]);
  and and_1 (isEqual, xnor_1_out, xnor_2_out);
endmodule

module _4_bit_equal (
  input  [3:0] A,
  input  [3:0] B,
  output isEqual
);

  wire xnor_1_out, xnor_2_out, xnor_3_out, xnor_4_out;

  xnor xnor_1 (xnor_1_out, A[0], B[0]);
  xnor xnor_2 (xnor_2_out, A[1], B[1]);
  xnor xnor_3 (xnor_3_out, A[2], B[2]);
  xnor xnor_4 (xnor_4_out, A[3], B[3]);
  and and_1 (isEqual, xnor_1_out, xnor_2_out, xnor_3_out, xnor_4_out);
endmodule

module _5_bit_equal (
  input  [4:0] A,
  input  [4:0] B,
  output isEqual
);

  wire xnor_1_out, xnor_2_out, xnor_3_out, xnor_4_out, xnor_5_out;

  xnor xnor_1 (xnor_1_out, A[0], B[0]);
  xnor xnor_2 (xnor_2_out, A[1], B[1]);
  xnor xnor_3 (xnor_3_out, A[2], B[2]);
  xnor xnor_4 (xnor_4_out, A[3], B[3]);
  xnor xnor_5 (xnor_5_out, A[4], B[4]);
  and and_1 (isEqual, xnor_1_out, xnor_2_out, xnor_3_out, xnor_4_out, xnor_5_out);
endmodule

module btn_id_4 (
  input  c0,
  input  c1,
  input  c2,
  input  c3,
  output [1:0] out,
  output btn_pressed
);

  assign out = c0 ? 2'b00 : 2'bz;  // Controlled_Buffer controlled_buffer_1
  assign out = c1 ? 2'b01 : 2'bz;  // Controlled_Buffer controlled_buffer_2
  assign out = c2 ? 2'b10 : 2'bz;  // Controlled_Buffer controlled_buffer_3
  assign out = c3 ? 2'b11 : 2'bz;  // Controlled_Buffer controlled_buffer_4
  or or_1 (btn_pressed, c0, c1, c2, c3);
endmodule

module btn_id_16 (
  input  c0,
  input  c1,
  input  c2,
  input  c3,
  input  c4,
  input  c5,
  input  c6,
  input  c7,
  input  c8,
  input  c9,
  input  c10,
  input  c11,
  input  c12,
  input  c13,
  input  c14,
  input  c15,
  output [3:0] out,
  output btn_pressed
);

  assign out = c0 ? 4'b0000 : 4'bz;  // Controlled_Buffer controlled_buffer_1
  assign out = c1 ? 4'b0001 : 4'bz;  // Controlled_Buffer controlled_buffer_2
  assign out = c2 ? 4'b0010 : 4'bz;  // Controlled_Buffer controlled_buffer_3
  assign out = c3 ? 4'b0011 : 4'bz;  // Controlled_Buffer controlled_buffer_4
  assign out = c4 ? 4'b0100 : 4'bz;  // Controlled_Buffer controlled_buffer_5
  assign out = c5 ? 4'b0101 : 4'bz;  // Controlled_Buffer controlled_buffer_6
  assign out = c6 ? 4'b0110 : 4'bz;  // Controlled_Buffer controlled_buffer_7
  assign out = c7 ? 4'b0111 : 4'bz;  // Controlled_Buffer controlled_buffer_8
  assign out = c8 ? 4'b1000 : 4'bz;  // Controlled_Buffer controlled_buffer_9
  assign out = c9 ? 4'b1001 : 4'bz;  // Controlled_Buffer controlled_buffer_10
  assign out = c10 ? 4'b1010 : 4'bz;  // Controlled_Buffer controlled_buffer_11
  assign out = c11 ? 4'b1011 : 4'bz;  // Controlled_Buffer controlled_buffer_12
  assign out = c12 ? 4'b1100 : 4'bz;  // Controlled_Buffer controlled_buffer_13
  assign out = c13 ? 4'b1101 : 4'bz;  // Controlled_Buffer controlled_buffer_14
  assign out = c14 ? 4'b1110 : 4'bz;  // Controlled_Buffer controlled_buffer_15
  assign out = c15 ? 4'b1111 : 4'bz;  // Controlled_Buffer controlled_buffer_16
  or or_1 (btn_pressed, c0, c1, c2, c3, c4, c5, c6, c7, c8, c9, c10, c11, c12, c13, c14, c15);
endmodule

module card_state (
  input  card_btn,
  input  reset,
  input  card_solved,
  output [1:0] card_state
);

  wire n2_bit_equal_1_isequal, not_1_out, or_1_out;
  wire [1:0] bit_extender_1_out, multiplexer_1_out;

  assign bit_extender_1_out = {{1{1'b0}}, card_btn};  // Bit_Extender bit_extender_1
  Multiplexer #(.width(2), .enable("false")) multiplexer_1 (
    .in0(bit_extender_1_out), .in1(2'b10), .out(multiplexer_1_out), .sel(card_solved));
  Register #(.width(2), .trigger("high")) register_1 (
    .D(multiplexer_1_out), .en(not_1_out), .Q(card_state), .clk(or_1_out), .clr(reset));
  not not_1 (not_1_out, n2_bit_equal_1_isequal);
  or or_1 (or_1_out, card_solved, card_btn);
  _2_bit_equal u_2_bit_equal_1 (.A(2'b00), .B(multiplexer_1_out), .isEqual(n2_bit_equal_1_isequal));

  // Notes on the sheet:
  //   once state set to solved, stuck
  //   change state when either button pressed or solved
endmodule

module timer (
  input  clk,
  input  clr,
  output [3:0] sec_d1,
  output [3:0] sec_d2,
  output [3:0] min_d1,
  output [3:0] min_d2
);

  wire minutes_d1_carry, minutes_d2_carry, or_1_out, or_2_out, or_3_out, or_4_out, seconds_d1_carry,
       seconds_d2_carry, ticks_carry;
  wire [2:0] minutes_d2_q, seconds_d2_q;

  Counter #(.width(5), .max('h18)) ticks (.count(clk), .carry(ticks_carry), .clk(clk), .clr(clr));  // open: load, D, Q
  Counter #(.width(4), .max('ha)) seconds_d1 (
    .count(ticks_carry), .Q(sec_d1), .carry(seconds_d1_carry), .clk(ticks_carry), .clr(or_1_out));  // open: load, D
  or or_1 (or_1_out, clr, seconds_d1_carry);
  Counter #(.width(3), .max('h6)) seconds_d2 (
    .count(seconds_d1_carry), .Q(seconds_d2_q), .carry(seconds_d2_carry), .clk(seconds_d1_carry),
    .clr(or_2_out));  // open: load, D
  or or_2 (or_2_out, clr, seconds_d2_carry);
  assign sec_d2 = {{1{1'b0}}, seconds_d2_q};  // Bit_Extender bit_extender_1
  Counter #(.width(4), .max('h9)) minutes_d1 (
    .count(seconds_d2_carry), .Q(min_d1), .carry(minutes_d1_carry), .clk(seconds_d2_carry), .clr(or_3_out));  // open: load, D
  or or_3 (or_3_out, clr, minutes_d1_carry);
  assign min_d2 = {{1{1'b0}}, minutes_d2_q};  // Bit_Extender bit_extender_2
  Counter #(.width(3), .max('h6)) minutes_d2 (
    .count(minutes_d1_carry), .Q(minutes_d2_q), .carry(minutes_d2_carry), .clk(minutes_d1_carry),
    .clr(or_4_out));  // open: load, D
  or or_4 (or_4_out, clr, minutes_d2_carry);

  // Other names for the same wires on the sheet: reset = clr
endmodule

module game_over (
  input  [15:0] \time ,
  input  reset,
  output game_over
);

  wire and_1_out, n4_bit_equal_1_isequal, n4_bit_equal_2_isequal, n4_bit_equal_3_isequal,
       n4_bit_equal_4_isequal;

  _4_bit_equal u_4_bit_equal_1 (.A(\time [3:0]), .B(4'b0000), .isEqual(n4_bit_equal_1_isequal));
  _4_bit_equal u_4_bit_equal_2 (.A(\time [7:4]), .B(4'b0000), .isEqual(n4_bit_equal_2_isequal));
  _4_bit_equal u_4_bit_equal_3 (.A(\time [11:8]), .B(4'b0010), .isEqual(n4_bit_equal_3_isequal));
  _4_bit_equal u_4_bit_equal_4 (.A(\time [15:12]), .B(4'b0000), .isEqual(n4_bit_equal_4_isequal));
  D_Flip_Flop #(.trigger("high")) d_ff_1 (
    .clk(and_1_out), .D(and_1_out), .Q(game_over), .en(and_1_out), .reset(reset));  // open: Qn, preset
  and and_1 (and_1_out, n4_bit_equal_1_isequal, n4_bit_equal_2_isequal, n4_bit_equal_3_isequal, n4_bit_equal_4_isequal);
endmodule

module winner (
  input  module_1,
  input  module_2,
  input  reset,
  output game_won
);

  wire and_1_out;

  and and_1 (and_1_out, module_1, module_2);
  D_Flip_Flop #(.trigger("high")) d_ff_1 (
    .clk(and_1_out), .D(and_1_out), .Q(game_won), .en(and_1_out), .reset(reset));  // open: Qn, preset
endmodule

module light_control (
  input  mode,
  input  [1:0] light_sel,
  input  b0,
  input  b1,
  input  b2,
  input  b3,
  output L0,
  output L1,
  output L2,
  output L3,
  output [1:0] btn,
  output btn_pressed
);

  wire and_1_out, and_2_out, and_3_out, and_4_out, and_5_out, and_6_out, and_7_out, and_8_out, in0, in1, in2,
       in3, showing_mode;

  Decoder #(.select(2)) decoder_1 (.out0(in0), .out1(in1), .out2(in2), .out3(in3), .sel(light_sel));  // open: en
  not not_1 (showing_mode, mode);
  btn_id_4 btn_id_4_1 (.c0(b0), .c1(b1), .c2(b2), .c3(b3), .out(btn), .btn_pressed(btn_pressed));
  and and_1 (and_1_out, showing_mode, in0);
  or or_1 (L0, and_1_out, and_2_out);
  and and_2 (and_2_out, mode, b0);
  and and_3 (and_3_out, showing_mode, in1);
  or or_2 (L1, and_3_out, and_4_out);
  and and_4 (and_4_out, mode, b1);
  and and_5 (and_5_out, showing_mode, in2);
  or or_3 (L2, and_5_out, and_6_out);
  and and_6 (and_6_out, mode, b2);
  and and_7 (and_7_out, showing_mode, in3);
  or or_4 (L3, and_7_out, and_8_out);
  and and_8 (and_8_out, mode, b3);

  // Other names for the same wires on the sheet: player_in_mode = mode
endmodule

module custom_counter (
  input  clk,
  input  in,
  input  en,
  input  clr,
  output [1:0] count
);

  wire and_1_out;

  T_Flip_Flop t_ff_1 (.clk(clk), .T(in), .Q(count[0]), .reset(clr), .en(en));  // open: Qn, preset
  and and_1 (and_1_out, count[0], in);
  T_Flip_Flop t_ff_2 (.clk(clk), .T(and_1_out), .Q(count[1]), .reset(clr), .en(en));  // open: Qn, preset
endmodule
